// Logisim project CPU_G8 (2).circ as structural Verilog
module main (
);

  wire add, add2, add3, add4, addi, addi2, addi3, addi4, and_1_out, branch, branch2, branch3, branch4, clk,
       execmem_1_memread_out_2, execmem_1_memtoreg_out_2, execmem_1_memwrite_out_2, execmem_1_regwrite_out_2,
       exhazard_1_forward, exhazard_1_forwarda, exhazard_1_forwardb, idec_exc_1_branch_out,
       idec_exc_1_memread_out, idec_exc_1_memtoreg_out, idec_exc_1_memwrite_out, idec_exc_1_regdst_out,
       idec_exc_1_regwrite_out, JUMP, jumpp2, jumpp3, jumpp4, k_1_r, load, load2, load3, load4,
       memhazard_1_forward, memhazard_1_forwarda, memhazard_1_forwardb, memwb_1_memtoreg_out_2,
       memwb_1_regwrite_out_3, not_1_out, Obranch, Ozero, reset, store, store2, store3, store4, uc_1_branch,
       uc_1_memread, uc_1_memtoreg, uc_1_memwrite, uc_1_regdest, uc_1_regwrite, zero;
  wire [1:0] ALUOp, idec_exc_1_aluop_out;
  wire [3:0] uca_1_out_3;
  wire [4:0] decodificador_1_shamt, execmem_1_out_25, ExMemRd, IdExRs, memwb_1_out_20, multiplexer_4_out,
       Ord, Ort, Orw, rd, rs, rt;
  wire [5:0] decodificador_1_funct, OP;
  wire [15:0] bit_extender_6_out, offset;
  wire [23:0] bit_extender_1_out, bit_extender_2_out, bit_extender_7_out, Branchadd, execmem_1_addbranch,
       execmem_1_pcinstr_2, idec_exc_1_out_43, if_dec_1_out_6, if_dec_1_out_8, memwb_1_out_30,
       multiplexer_1_out, multiplexer_2_out, Opc, pc;
  wire [25:0] jump_t;
  wire [31:0] adder_1_out, ALUSUMA, bit_extender_5_out, execmem_1_addbranch_2, execmem_1_oalusuma,
       idec_exc_1_data1, idec_exc_1_data2, idec_exc_1_offset_2, if_dec_1_out_7, memwb_1_out_17,
       memwb_1_out_18, mostrarinst_1_out_7, mostrarinst_1_out_8, mostrarinst_1_out_9, mostrarinst_1_out_10,
       mostrarinst_1_out_11, mostrarinst_2_out_7, mostrarinst_2_out_8, mostrarinst_2_out_9,
       mostrarinst_2_out_10, mostrarinst_2_out_11, mostrarinst_3_out_7, mostrarinst_3_out_8,
       mostrarinst_3_out_9, mostrarinst_3_out_10, mostrarinst_3_out_11, mostrarinst_4_out_7,
       mostrarinst_4_out_8, mostrarinst_4_out_9, mostrarinst_4_out_10, mostrarinst_4_out_11,
       multiplexer_3_out, NPC, OData, OData2, ram_1_data, ram_2_data, register_1_q, UnidadRegistros_out_7,
       UnidadRegistros_out_8;

  Multiplexer #(.width(24)) multiplexer_1 (
    .in0(pc), .in1(execmem_1_addbranch), .out(multiplexer_1_out), .sel(and_1_out));  // open: en
  and and_1 (and_1_out, Ozero, Obranch);
  Bit_Extender #(.in_width(26), .out_width(24)) bit_extender_1 (.in(jump_t), .out(bit_extender_1_out));
  Register #(.width(32)) register_1 (.D(NPC), .en(1'b1), .Q(register_1_q), .clk(clk), .clr(reset));
  Adder #(.width(32)) adder_1 (.a(register_1_q), .b(32'h1), .out(adder_1_out));  // open: cin, cout
  Bit_Extender #(.in_width(32), .out_width(24)) bit_extender_2 (.in(register_1_q), .out(bit_extender_2_out));
  Multiplexer #(.width(24)) multiplexer_2 (
    .in0(multiplexer_1_out), .in1(bit_extender_1_out), .out(multiplexer_2_out), .sel(JUMP));  // open: en
  mostrarInst mostrarinst_1 (
    .ADD(add), .LOAD(load), .STORE(store), .BRANCH(branch), .JUMP(JUMP), .ADDI(addi),
    .out_7(mostrarinst_1_out_7), .out_8(mostrarinst_1_out_8), .out_9(mostrarinst_1_out_9),
    .out_10(mostrarinst_1_out_10), .out_11(mostrarinst_1_out_11));
  DotMatrix #(.inputtype("row"), .matrixcols(32), .matrixrows(5)) dotmatrix_1 (
    .row0(mostrarinst_1_out_7), .row1(mostrarinst_1_out_8), .row2(mostrarinst_1_out_9),
    .row3(mostrarinst_1_out_10), .row4(mostrarinst_1_out_11));
  Bit_Extender #(.in_width(32), .out_width(24)) bit_extender_3 (.in(adder_1_out), .out(pc));
  assign NPC = {{8{1'b0}}, multiplexer_2_out};  // Bit_Extender bit_extender_4
  // Probe on bit_extender_2_out
  Clock clock_1 (.out(clk));
  Button button_1 (.out(reset));
  IF_Dec if_dec_1 (
    .in_1(clk), .in_2(reset), .Instr(ram_1_data), .out_7(if_dec_1_out_7), .Pc_1(pc), .out_6(if_dec_1_out_6),
    .Pc_instr(bit_extender_2_out), .out_8(if_dec_1_out_8));
  RAM #(.addrWidth(24), .dataWidth(32)) ram_1 (
    .addr(bit_extender_2_out), .data(ram_1_data));  // open: sel, clk, ld, clr
  decodificador decodificador_1 (
    .in_1(if_dec_1_out_7), .Funct(decodificador_1_funct), .Shamt(decodificador_1_shamt), .RD(rd), .RT(rt),
    .RS(rs), .out_7(OP), .out_8(offset), .out_9(jump_t));
  // Probe on decodificador_1_funct
  // Probe on OP
  // Probe on jump_t
  UCA uca_1 (.ALUOp(ALUOp), .Func(decodificador_1_funct), .out_3(uca_1_out_3));
  // Probe on uca_1_out_3
  // Probe on decodificador_1_shamt
  // Probe on rd
  // Probe on rt
  // Probe on rs
  // Probe on offset
  // Probe on if_dec_1_out_8
  k k_1 (.in_1(OP), .r(k_1_r), .Add(add), .load(load), .store(store), .branch(branch), .jump(JUMP));
  LED R (.in(k_1_r));
  LED u_ADD (.in(add));
  LED u_LOAD (.in(load));
  LED u_STORE (.in(store));
  LED u_BRANCH (.in(branch));
  LED JUMP_2 (.in(JUMP));
  UC uc_1 (
    .in_1(OP), .RegDest(uc_1_regdest), .ALUsrc(addi), .MemtoReg(uc_1_memtoreg), .RegWrite(uc_1_regwrite),
    .MemRead(uc_1_memread), .MemWrite(uc_1_memwrite), .Branch(uc_1_branch), .out_9(ALUOp));
  UnidadRegistros UnidadRegistros (
    .rs(rs), .rt(rt), .rw(Orw), .in_4(OData), .in_5(clk), .in_6(reset), .out_7(UnidadRegistros_out_7),
    .out_8(UnidadRegistros_out_8));
  DotMatrix #(.inputtype("row"), .matrixcols(32), .matrixrows(5)) dotmatrix_2 (
    .row0(mostrarinst_2_out_7), .row1(mostrarinst_2_out_8), .row2(mostrarinst_2_out_9),
    .row3(mostrarinst_2_out_10), .row4(mostrarinst_2_out_11));
  mostrarInst mostrarinst_2 (
    .ADD(add2), .LOAD(load2), .STORE(store2), .BRANCH(branch2), .JUMP(jumpp2), .ADDI(addi2),
    .out_7(mostrarinst_2_out_7), .out_8(mostrarinst_2_out_8), .out_9(mostrarinst_2_out_9),
    .out_10(mostrarinst_2_out_10), .out_11(mostrarinst_2_out_11));
  IDec_Exc idec_exc_1 (
    .in_1(clk), .in_2(reset), .Pc_1(if_dec_1_out_6), .pc_1_2(Opc), .Data1RS(UnidadRegistros_out_7),
    .Data1(idec_exc_1_data1), .Data2RT(UnidadRegistros_out_8), .Data2(idec_exc_1_data2),
    .offset(bit_extender_5_out), .offset_2(idec_exc_1_offset_2), .Pc_instr(if_dec_1_out_8),
    .out_43(idec_exc_1_out_43), .in_7(rt), .in_8(rd), .out_28(Ort), .out_29(Ord), .RegDst_in(uc_1_regdest),
    .RegDst_out(idec_exc_1_regdst_out), .ALUsrc_in(addi), .ALUsrc_out(addi2), .MemToReg_in(uc_1_memtoreg),
    .MemToReg_out(idec_exc_1_memtoreg_out), .RegWrite_in(uc_1_regwrite),
    .RegWrite_out(idec_exc_1_regwrite_out), .MemRead_in(uc_1_memread), .MemRead_out(idec_exc_1_memread_out),
    .MemWrite_in(uc_1_memwrite), .MemWrite_out(idec_exc_1_memwrite_out), .Branch_in(uc_1_branch),
    .Branch_out(idec_exc_1_branch_out), .ALUOp_in(ALUOp), .ALUOp_out(idec_exc_1_aluop_out), .rs(rs),
    .rs_2(IdExRs), .RegDst_in_2(add), .RegDst_out_2(add2), .ALUsrc_in_2(load), .ALUsrc_out_2(load2),
    .MemToReg_in_2(store), .MemToReg_out_2(store2), .RegWrite_in_2(branch), .RegWrite_out_2(branch2),
    .MemRead_in_2(JUMP), .MemRead_out_2(jumpp2));
  assign bit_extender_5_out = {{16{1'b0}}, offset};  // Bit_Extender bit_extender_5
  // Probe on idec_exc_1_out_43
  Multiplexer #(.width(32)) multiplexer_3 (
    .in0(idec_exc_1_data2), .in1(idec_exc_1_offset_2), .out(multiplexer_3_out), .sel(addi2));  // open: en
  Comparator #(.width(32)) comparator_1 (.a(idec_exc_1_data1), .b(idec_exc_1_data2), .eq(zero));  // open: gt, lt
  Adder #(.width(32)) adder_2 (.a(idec_exc_1_data1), .b(multiplexer_3_out), .out(ALUSUMA));  // open: cin, cout
  branch branch_2 (.offset(bit_extender_6_out), .out_3(Branchadd), .pc(Opc));
  Bit_Extender #(.in_width(32)) bit_extender_6 (.in(idec_exc_1_offset_2), .out(bit_extender_6_out));
  DotMatrix #(.inputtype("row"), .matrixcols(32), .matrixrows(5)) dotmatrix_3 (
    .row0(mostrarinst_3_out_7), .row1(mostrarinst_3_out_8), .row2(mostrarinst_3_out_9),
    .row3(mostrarinst_3_out_10), .row4(mostrarinst_3_out_11));
  mostrarInst mostrarinst_3 (
    .ADD(add3), .LOAD(load3), .STORE(store3), .BRANCH(branch3), .JUMP(jumpp3), .ADDI(addi3),
    .out_7(mostrarinst_3_out_7), .out_8(mostrarinst_3_out_8), .out_9(mostrarinst_3_out_9),
    .out_10(mostrarinst_3_out_10), .out_11(mostrarinst_3_out_11));
  Multiplexer #(.width(5)) multiplexer_4 (.in0(Ord), .in1(Ort), .out(multiplexer_4_out), .sel(addi2));  // open: en
  ExecMem execmem_1 (
    .in_3(Branchadd), .AddBranch(execmem_1_addbranch), .zero(zero), .Ozero(Ozero), .ALUSUMA(ALUSUMA),
    .OALUSUMA(execmem_1_oalusuma), .in_6(OData2), .AddBranch_2(execmem_1_addbranch_2),
    .PCinstr(idec_exc_1_out_43), .PCinstr_2(execmem_1_pcinstr_2), .in_1(clk), .in_2(reset),
    .in_7(multiplexer_4_out), .out_25(execmem_1_out_25), .MemToReg_in_2(idec_exc_1_memtoreg_out),
    .MemToReg_out_2(execmem_1_memtoreg_out_2), .RegWrite_in_2(idec_exc_1_regwrite_out),
    .RegWrite_out_2(execmem_1_regwrite_out_2), .MemRead_in_2(idec_exc_1_memread_out),
    .MemRead_out_2(execmem_1_memread_out_2), .MemWrite_in_2(idec_exc_1_memwrite_out),
    .MemWrite_out_2(execmem_1_memwrite_out_2), .Branch_in_2(idec_exc_1_branch_out), .Branch_out_2(Obranch),
    .rd(Ord), .rd_2(ExMemRd), .MemToReg_in(add2), .MemToReg_out(add3), .RegWrite_in(load2),
    .RegWrite_out(load3), .MemRead_in(store2), .MemRead_out(store3), .MemWrite_in(branch2),
    .MemWrite_out(branch3), .Branch_in(jumpp2), .Branch_out(jumpp3), .Branch_in_3(addi2), .Branch_out_3(addi3));
  Bit_Extender #(.in_width(32), .out_width(24)) bit_extender_7 (.in(execmem_1_oalusuma), .out(bit_extender_7_out));
  // Probe on execmem_1_pcinstr_2
  LED ForwardA (.in(exhazard_1_forwarda));
  ExHazard exhazard_1 (
    .ExMemRegWr(execmem_1_regwrite_out_2), .ExMemRd(ExMemRd), .IDExcRs(IdExRs), .IDExcRt(Ort),
    .forward(exhazard_1_forward), .ForwardA(exhazard_1_forwarda), .ForwardB(exhazard_1_forwardb));
  LED Forward (.in(exhazard_1_forward));
  LED ForwardB (.in(exhazard_1_forwardb));
  not not_1 (not_1_out, execmem_1_memwrite_out_2);
  RAM #(.addrWidth(24), .dataWidth(32), .bus("separate")) ram_2 (
    .addr(bit_extender_7_out), .din(execmem_1_addbranch_2), .data(ram_2_data), .clk(clk), .ld(not_1_out),
    .clr(reset));  // open: str, sel
  mostrarInst mostrarinst_4 (
    .ADD(add4), .LOAD(load4), .STORE(store4), .BRANCH(branch4), .JUMP(jumpp4), .ADDI(addi4),
    .out_7(mostrarinst_4_out_7), .out_8(mostrarinst_4_out_8), .out_9(mostrarinst_4_out_9),
    .out_10(mostrarinst_4_out_10), .out_11(mostrarinst_4_out_11));
  DotMatrix #(.inputtype("row"), .matrixcols(32), .matrixrows(5)) dotmatrix_4 (
    .row0(mostrarinst_4_out_7), .row1(mostrarinst_4_out_8), .row2(mostrarinst_4_out_9),
    .row3(mostrarinst_4_out_10), .row4(mostrarinst_4_out_11));
  MemWB memwb_1 (
    .in_4(execmem_1_oalusuma), .out_18(memwb_1_out_18), .in_3(ram_2_data), .out_17(memwb_1_out_17),
    .in_16(execmem_1_pcinstr_2), .out_30(memwb_1_out_30), .in_1(clk), .in_2(reset), .in_5(execmem_1_out_25),
    .out_19(Orw), .MemToReg_in_2(execmem_1_memtoreg_out_2), .MemToReg_out_2(memwb_1_memtoreg_out_2),
    .RegWrite_in_3(execmem_1_regwrite_out_2), .RegWrite_out_3(memwb_1_regwrite_out_3),
    .MemRead_in_3(execmem_1_memread_out_2), .in_6(ExMemRd), .out_20(memwb_1_out_20), .MemToReg_in(add3),
    .MemToReg_out(add4), .RegWrite_in(load3), .RegWrite_out(load4), .MemRead_in(store3),
    .MemRead_out(store4), .RegWrite_in_2(branch3), .RegWrite_out_2(branch4), .MemRead_in_2(jumpp3),
    .MemRead_in_4(addi3), .MemRead_out_4(addi4));  // open: MemRead_out_3, MemRead_out_2
  // Probe on memwb_1_out_30
  Multiplexer #(.width(32)) multiplexer_5 (
    .in0(memwb_1_out_18), .in1(memwb_1_out_17), .out(OData), .sel(memwb_1_memtoreg_out_2));  // open: en
  LED ForwardA_2 (.in(memhazard_1_forwarda));
  LED Forward_2 (.in(memhazard_1_forward));
  MemHazard memhazard_1 (
    .MemWbRegWr(memwb_1_regwrite_out_3), .MemWbRd(memwb_1_out_20), .ExMemRd(ExMemRd), .IdExRs(IdExRs),
    .IdExRt(Ort), .Forward(memhazard_1_forward), .ForwardA(memhazard_1_forwarda),
    .ForwardB(memhazard_1_forwardb));
  LED ForwardB_2 (.in(memhazard_1_forwardb));

  // Other names for the same wires on the sheet: jumpp = JUMP

  // Notes on the sheet:
  //   Funct
  //   Shamt
  //   Rd
  //   Rt
  //   RS
  //   OP
  //   Offset
  //   RegDest
  //   ALUsrc
  //   MToReg
  //   RegWr
  //   MemRead
  //   MemWR
  //   Branch
  //   ALUOp
  //   Data1
  //   Data 2
  //   Offset
  //   ALUsrc
  //   BranchAdd
  //   BranchAdd
  //   ALUSUMA
  //   Data2
  //   MemWR
  //   ReadData
  //   ReadData
  //   ALUSUMA
  //   MToReg
endmodule

// Spliter
module decodificador (
  input  [31:0] in_1,
  output [5:0] Funct,
  output [4:0] Shamt,
  output [4:0] RD,
  output [4:0] RT,
  output [4:0] RS,
  output [5:0] out_7,
  output [15:0] out_8,
  output [25:0] out_9
);


  assign Funct = in_1[5:0];
  assign out_7 = in_1[31:26];
  assign out_8 = in_1[15:0];
  assign out_9 = in_1[25:0];
  assign RD = in_1[15:11];
  assign RS = in_1[25:21];
  assign RT = in_1[20:16];
  assign Shamt = in_1[10:6];

  // Notes on the sheet:
  //   R
  //   Branch
  //   Jump
  //   OP Code
  //   Offset
  //   Jump
endmodule

module k (
  input  [5:0] in_1,
  output r,
  output Add,
  output load,
  output store,
  output branch,
  output jump
);

  Comparator #(.width(6)) comparator_1 (.a(in_1), .b({6{1'b0}}), .eq(r));  // open: gt, lt
  Comparator #(.width(6)) comparator_2 (.a(in_1), .b({6{1'b0}}), .eq(Add));  // open: gt, lt
  Comparator #(.width(6)) comparator_3 (.a(in_1), .b(6'b100011), .eq(load));  // open: gt, lt
  Comparator #(.width(6)) comparator_4 (.a(in_1), .b(6'b101011), .eq(store));  // open: gt, lt
  Comparator #(.width(6)) comparator_5 (.a(in_1), .b(6'b000100), .eq(branch));  // open: gt, lt
  Comparator #(.width(6)) comparator_6 (.a(in_1), .b(6'b000010), .eq(jump));  // open: gt, lt
endmodule

// UR
module UnidadRegistros (
  input  [4:0] rs,
  input  [4:0] rt,
  input  [4:0] rw,
  input  [31:0] in_4,
  input  in_5,
  input  in_6,
  output [31:0] out_7,
  output [31:0] out_8
);

  wire B0, B1, B2, B3, B4, B5, B6, B7, B8, B9, B10, B11, B12, B13, B14, B15, B16, B17, B18, B19, B20, B21,
       B22, B23, B24, B25, B26, B27, B28, B29, B30, B31;
  wire [31:0] _0, _1, _2, _3, _4, _5, _6, _7, _8, _9, _10, _11, _12, _13, _14, _15, _16, _17, _18, _19, _20,
       _21, _22, _23, _24, _25, _26, _27, _28, _29, _30, _31, r0, r1, r2, r3, r4, r5, r6, r7, r8, r9, r10,
       r11, r12, r13, r14, r15, r16, r17, r18, r19, r20, r21, r22, r23, r24, r25, r26, r27, r28, r29, r30,
       r31;

  Register #(.width(32)) register_1 (.D(_0), .en(B0), .Q(r0), .clk(in_5), .clr(in_6));
  Register #(.width(32)) register_2 (.D(_1), .en(B1), .Q(r1), .clk(in_5), .clr(in_6));
  Register #(.width(32)) register_3 (.D(_2), .en(B2), .Q(r2), .clk(in_5), .clr(in_6));
  Register #(.width(32)) register_4 (.D(_3), .en(B3), .Q(r3), .clk(in_5), .clr(in_6));
  Register #(.width(32)) register_5 (.D(_4), .en(B4), .Q(r4), .clk(in_5), .clr(in_6));
  Register #(.width(32)) register_6 (.D(_5), .en(B5), .Q(r5), .clk(in_5), .clr(in_6));
  Register #(.width(32)) register_7 (.D(_6), .en(B6), .Q(r6), .clk(in_5), .clr(in_6));
  Register #(.width(32)) register_8 (.D(_7), .en(B7), .Q(r7), .clk(in_5), .clr(in_6));
  Register #(.width(32)) register_9 (.D(_8), .en(B8), .Q(r8), .clk(in_5), .clr(in_6));
  Register #(.width(32)) register_10 (.D(_9), .en(B9), .Q(r9), .clk(in_5), .clr(in_6));
  Register #(.width(32)) register_11 (.D(_10), .en(B10), .Q(r10), .clk(in_5), .clr(in_6));
  Register #(.width(32)) register_12 (.D(_11), .en(B11), .Q(r11), .clk(in_5), .clr(in_6));
  Register #(.width(32)) register_13 (.D(_12), .en(B12), .Q(r12), .clk(in_5), .clr(in_6));
  Register #(.width(32)) register_14 (.D(_13), .en(B13), .Q(r13), .clk(in_5), .clr(in_6));
  Register #(.width(32)) register_15 (.D(_14), .en(B14), .Q(r14), .clk(in_5), .clr(in_6));
  Register #(.width(32)) register_16 (.D(_15), .en(B15), .Q(r15), .clk(in_5), .clr(in_6));
  // Probe on nothing
  Register #(.width(32)) register_17 (.D(_16), .en(B16), .Q(r16), .clk(in_5), .clr(in_6));
  Register #(.width(32)) register_18 (.D(_17), .en(B17), .Q(r17), .clk(in_5), .clr(in_6));
  Register #(.width(32)) register_19 (.D(_18), .en(B18), .Q(r18), .clk(in_5), .clr(in_6));
  Register #(.width(32)) register_20 (.D(_19), .en(B19), .Q(r19), .clk(in_5), .clr(in_6));
  Register #(.width(32)) register_21 (.D(_20), .en(B20), .Q(r20), .clk(in_5), .clr(in_6));
  Register #(.width(32)) register_22 (.D(_21), .en(B21), .Q(r21), .clk(in_5), .clr(in_6));
  Register #(.width(32)) register_23 (.D(_22), .en(B22), .Q(r22), .clk(in_5), .clr(in_6));
  Register #(.width(32)) register_24 (.D(_23), .en(B23), .Q(r23), .clk(in_5), .clr(in_6));
  Register #(.width(32)) register_25 (.D(_24), .en(B24), .Q(r24), .clk(in_5), .clr(in_6));
  Register #(.width(32)) register_26 (.D(_25), .en(B25), .Q(r25), .clk(in_5), .clr(in_6));
  Register #(.width(32)) register_27 (.D(_26), .en(B26), .Q(r26), .clk(in_5), .clr(in_6));
  Register #(.width(32)) register_28 (.D(_27), .en(B27), .Q(r27), .clk(in_5), .clr(in_6));
  Register #(.width(32)) register_29 (.D(_28), .en(B28), .Q(r28), .clk(in_5), .clr(in_6));
  Register #(.width(32)) register_30 (.D(_29), .en(B29), .Q(r29), .clk(in_5), .clr(in_6));
  Register #(.width(32)) register_31 (.D(_30), .en(B30), .Q(r30), .clk(in_5), .clr(in_6));
  Register #(.width(32)) register_32 (.D(_31), .en(B31), .Q(r31), .clk(in_5), .clr(in_6));
  Multiplexer #(.select(5), .width(32)) multiplexer_1 (
    .in0(r0), .in1(r1), .in2(r2), .in3(r3), .in4(r4), .in5(r5), .in6(r6), .in7(r7), .in8(r8), .in9(r9),
    .in10(r10), .in11(r11), .in12(r12), .in13(r13), .in14(r14), .in15(r15), .in16(r16), .in17(r17),
    .in18(r18), .in19(r19), .in20(r20), .in21(r21), .in22(r22), .in23(r23), .in24(r24), .in25(r25),
    .in26(r26), .in27(r27), .in28(r28), .in29(r29), .in30(r30), .in31(r31), .out(out_7), .sel(rs));  // open: en
  Multiplexer #(.select(5), .width(32)) multiplexer_2 (
    .in0(r0), .in1(r1), .in2(r2), .in3(r3), .in4(r4), .in5(r5), .in6(r6), .in7(r7), .in8(r8), .in9(r9),
    .in10(r10), .in11(r11), .in12(r12), .in13(r13), .in14(r14), .in15(r15), .in16(r16), .in17(r17),
    .in18(r18), .in19(r19), .in20(r20), .in21(r21), .in22(r22), .in23(r23), .in24(r24), .in25(r25),
    .in26(r26), .in27(r27), .in28(r28), .in29(r29), .in30(r30), .in31(r31), .out(out_8), .sel(rt));  // open: en
  Demultiplexer #(.select(5)) demultiplexer_1 (
    .out0(B0), .out1(B1), .out2(B2), .out3(B3), .out4(B4), .out5(B5), .out6(B6), .out7(B7), .out8(B8),
    .out9(B9), .out10(B10), .out11(B11), .out12(B12), .out13(B13), .out14(B14), .out15(B15), .out16(B16),
    .out17(B17), .out18(B18), .out19(B19), .out20(B20), .out21(B21), .out22(B22), .out23(B23), .out24(B24),
    .out25(B25), .out26(B26), .out27(B27), .out28(B28), .out29(B29), .out30(B30), .out31(B31), .in(1'b1),
    .sel(rw));  // open: en
  Demultiplexer #(.select(5), .width(32)) demultiplexer_2 (
    .out0(_0), .out1(_1), .out2(_2), .out3(_3), .out4(_4), .out5(_5), .out6(_6), .out7(_7), .out8(_8),
    .out9(_9), .out10(_10), .out11(_11), .out12(_12), .out13(_13), .out14(_14), .out15(_15), .out16(_16),
    .out17(_17), .out18(_18), .out19(_19), .out20(_20), .out21(_21), .out22(_22), .out23(_23), .out24(_24),
    .out25(_25), .out26(_26), .out27(_27), .out28(_28), .out29(_29), .out30(_30), .out31(_31), .in(in_4),
    .sel(rw));  // open: en

  // Other names for the same wires on the sheet: clk = in_5; Data[31:0] = in_4; reset = in_6
endmodule

module UC (
  input  [5:0] in_1,
  output RegDest,
  output ALUsrc,
  output MemtoReg,
  output RegWrite,
  output MemRead,
  output MemWrite,
  output Branch,
  output [1:0] out_9
);

  wire and_4_out, and_5_out, not_2_out, not_3_out, not_4_out, not_5_out, not_6_out, not_7_out, not_8_out;

  not not_1 (RegDest, in_1[5]);
  or or_1 (ALUsrc, in_1[1], in_1[3]);
  not not_2 (not_2_out, in_1[2]);
  not not_3 (not_3_out, in_1[3]);
  not not_4 (not_4_out, in_1[2]);
  not not_5 (not_5_out, in_1[5]);
  and and_1 (MemRead, in_1[1], not_6_out);
  not not_6 (not_6_out, in_1[3]);
  and and_2 (MemWrite, in_1[3], in_1[0]);
  not not_7 (not_7_out, in_1[2]);
  and and_3 (out_9[1], not_7_out, not_8_out);
  not not_8 (not_8_out, in_1[5]);
  and and_4 (and_4_out, not_2_out, not_3_out);
  and and_5 (and_5_out, not_4_out, not_5_out);
  or or_2 (RegWrite, and_4_out, and_5_out);

  assign Branch = in_1[2];
  assign MemtoReg = in_1[1];
  assign out_9[0] = in_1[2];
endmodule

module UCA (
  input  [1:0] ALUOp,
  input  [5:0] Func,
  output [3:0] out_3
);

  wire and_1_out, and_2_out, and_3_out, and_4_out, not_1_out, not_2_out, not_3_out;

  not not_1 (not_1_out, ALUOp[0]);
  not not_2 (not_2_out, ALUOp[0]);
  not not_3 (not_3_out, Func[2]);
  and and_1 (and_1_out, ALUOp[0], Func[0]);
  and and_2 (and_2_out, ALUOp[0], Func[3]);
  and and_3 (and_3_out, not_1_out, ALUOp[1]);
  and and_4 (and_4_out, ALUOp[0], Func[1]);
  or or_1 (out_3[1], not_2_out, not_3_out);
  or or_2 (out_3[0], and_1_out, and_2_out);
  or or_3 (out_3[2], and_3_out, and_4_out);

  assign out_3[3] = 1'b0;
endmodule

// Branch
module branch (
  input  [23:0] pc,
  input  [15:0] offset,
  output [23:0] out_3
);

  wire [23:0] adder_1_out, bit_extender_1_out, subtractor_1_out;

  assign bit_extender_1_out = {{9{1'b0}}, offset[14:0]};  // Bit_Extender bit_extender_1
  Adder #(.width(24)) adder_1 (.a(pc), .b(bit_extender_1_out), .out(adder_1_out));  // open: cin, cout
  Subtractor #(.width(24)) subtractor_1 (.a(pc), .b(bit_extender_1_out), .out(subtractor_1_out));  // open: bin, bout
  Multiplexer #(.width(24)) multiplexer_1 (
    .in0(adder_1_out), .in1(subtractor_1_out), .out(out_3), .sel(offset[15]));  // open: en
endmodule

module IF_Dec (
  input  in_1,
  input  in_2,
  input  [23:0] Pc_1,
  input  [31:0] Instr,
  input  [23:0] Pc_instr,
  output [23:0] out_6,
  output [31:0] out_7,
  output [23:0] out_8
);

  Register #(.width(24)) u_PC_1 (.D(Pc_1), .Q(out_6), .clk(in_1), .clr(in_2));  // open: en
  Register #(.width(32)) u_Instr (.D(Instr), .Q(out_7), .clk(in_1), .clr(in_2));  // open: en
  Register #(.width(24)) PC_Ins (.D(Pc_instr), .Q(out_8), .clk(in_1), .clr(in_2));  // open: en

  // Other names for the same wires on the sheet: clk = in_1; reset = in_2
endmodule

module IDec_Exc (
  input  in_1,
  input  in_2,
  input  [23:0] Pc_1,
  input  [31:0] Data1RS,
  input  [31:0] Data2RT,
  input  [31:0] offset,
  input  [4:0] in_7,
  input  [4:0] in_8,
  input  [4:0] rs,
  input  RegDst_in,
  input  RegDst_in_2,
  input  ALUsrc_in,
  input  ALUsrc_in_2,
  input  MemToReg_in,
  input  MemToReg_in_2,
  input  RegWrite_in,
  input  RegWrite_in_2,
  input  MemRead_in,
  input  MemRead_in_2,
  input  MemWrite_in,
  input  Branch_in,
  input  [23:0] Pc_instr,
  input  [1:0] ALUOp_in,
  output [23:0] pc_1_2,
  output [31:0] Data1,
  output [31:0] Data2,
  output [31:0] offset_2,
  output [4:0] out_28,
  output [4:0] out_29,
  output [4:0] rs_2,
  output RegDst_out,
  output RegDst_out_2,
  output ALUsrc_out,
  output ALUsrc_out_2,
  output MemToReg_out,
  output MemToReg_out_2,
  output RegWrite_out,
  output RegWrite_out_2,
  output MemRead_out,
  output MemRead_out_2,
  output MemWrite_out,
  output Branch_out,
  output [23:0] out_43,
  output [1:0] ALUOp_out
);

  Register #(.width(24)) u_PC_1 (.D(Pc_1), .Q(pc_1_2), .clk(in_1), .clr(in_2));  // open: en
  Register #(.width(32)) dataRS (.D(Data1RS), .Q(Data1), .clk(in_1), .clr(in_2));  // open: en
  Register #(.width(32)) dataRT (.D(Data2RT), .Q(Data2), .clk(in_1), .clr(in_2));  // open: en
  Register #(.width(32)) u_offset (.D(offset), .Q(offset_2), .clk(in_1), .clr(in_2));  // open: en
  Register #(.width(5)) register_1 (.D(in_7), .Q(out_28), .clk(in_1), .clr(in_2));  // open: en
  Register #(.width(5)) register_2 (.D(in_8), .Q(out_29), .clk(in_1), .clr(in_2));  // open: en
  Register #(.width(5)) u_rs (.D(rs), .Q(rs_2), .clk(in_1), .clr(in_2));  // open: en
  Register #(.width(1)) register_3 (.D(RegDst_in), .Q(RegDst_out), .clk(in_1), .clr(in_2));  // open: en
  Register #(.width(1)) register_4 (.D(ALUsrc_in), .Q(ALUsrc_out), .clk(in_1), .clr(in_2));  // open: en
  Register #(.width(1)) register_5 (.D(MemToReg_in), .Q(MemToReg_out), .clk(in_1), .clr(in_2));  // open: en
  Register #(.width(1)) register_6 (.D(RegWrite_in), .Q(RegWrite_out), .clk(in_1), .clr(in_2));  // open: en
  Register #(.width(1)) register_7 (.D(MemRead_in), .Q(MemRead_out), .clk(in_1), .clr(in_2));  // open: en
  Register #(.width(1)) register_8 (.D(MemWrite_in), .Q(MemWrite_out), .clk(in_1), .clr(in_2));  // open: en
  Register #(.width(1)) register_9 (.D(Branch_in), .Q(Branch_out), .clk(in_1), .clr(in_2));  // open: en
  Register #(.width(24)) PC_Ins (.D(Pc_instr), .en(in_1), .Q(out_43), .clk(in_1), .clr(in_2));
  Register #(.width(2)) register_10 (.D(ALUOp_in), .Q(ALUOp_out), .clk(in_1), .clr(in_2));  // open: en
  Register #(.width(1)) register_11 (.D(RegDst_in_2), .Q(RegDst_out_2), .clk(in_1), .clr(in_2));  // open: en
  Register #(.width(1)) register_12 (.D(ALUsrc_in_2), .Q(ALUsrc_out_2), .clk(in_1), .clr(in_2));  // open: en
  Register #(.width(1)) register_13 (.D(MemToReg_in_2), .Q(MemToReg_out_2), .clk(in_1), .clr(in_2));  // open: en
  Register #(.width(1)) register_14 (.D(RegWrite_in_2), .Q(RegWrite_out_2), .clk(in_1), .clr(in_2));  // open: en
  Register #(.width(1)) register_15 (.D(MemRead_in_2), .Q(MemRead_out_2), .clk(in_1), .clr(in_2));  // open: en

  // Other names for the same wires on the sheet: clk = in_1; reset = in_2
endmodule

module ExecMem (
  input  in_1,
  input  in_2,
  input  [23:0] in_3,
  input  zero,
  input  [31:0] ALUSUMA,
  input  [31:0] in_6,
  input  [4:0] in_7,
  input  [4:0] rd,
  input  MemToReg_in,
  input  RegWrite_in,
  input  MemRead_in,
  input  MemWrite_in,
  input  Branch_in,
  input  MemToReg_in_2,
  input  RegWrite_in_2,
  input  MemRead_in_2,
  input  MemWrite_in_2,
  input  Branch_in_2,
  input  Branch_in_3,
  input  [23:0] PCinstr,
  output [23:0] AddBranch,
  output Ozero,
  output [31:0] OALUSUMA,
  output [31:0] AddBranch_2,
  output [4:0] out_25,
  output [4:0] rd_2,
  output MemToReg_out,
  output RegWrite_out,
  output MemRead_out,
  output MemWrite_out,
  output Branch_out,
  output MemToReg_out_2,
  output RegWrite_out_2,
  output MemRead_out_2,
  output MemWrite_out_2,
  output Branch_out_2,
  output Branch_out_3,
  output [23:0] PCinstr_2
);

  Register #(.width(24)) u_AddBranch (.D(in_3), .Q(AddBranch), .clk(in_1), .clr(in_2));  // open: en
  Register #(.width(1)) u_zero (.D(zero), .Q(Ozero), .clk(in_1), .clr(in_2));  // open: en
  Register #(.width(32)) u_ALUSUMA (.D(ALUSUMA), .Q(OALUSUMA), .clk(in_1), .clr(in_2));  // open: en
  Register #(.width(32)) u_AddBranch_2 (.D(in_6), .Q(AddBranch_2), .clk(in_1), .clr(in_2));  // open: en
  Register #(.width(5)) register_1 (.D(in_7), .Q(out_25), .clk(in_1), .clr(in_2));  // open: en
  Register #(.width(5)) u_rd (.D(rd), .Q(rd_2), .clk(in_1), .clr(in_2));  // open: en
  Register #(.width(1)) register_2 (.D(MemToReg_in), .Q(MemToReg_out), .clk(in_1), .clr(in_2));  // open: en
  Register #(.width(1)) register_3 (.D(RegWrite_in), .Q(RegWrite_out), .clk(in_1), .clr(in_2));  // open: en
  Register #(.width(1)) register_4 (.D(MemRead_in), .Q(MemRead_out), .clk(in_1), .clr(in_2));  // open: en
  Register #(.width(1)) register_5 (.D(MemWrite_in), .Q(MemWrite_out), .clk(in_1), .clr(in_2));  // open: en
  Register #(.width(1)) register_6 (.D(Branch_in), .Q(Branch_out), .clk(in_1), .clr(in_2));  // open: en
  Register #(.width(1)) register_7 (.D(MemToReg_in_2), .Q(MemToReg_out_2), .clk(in_1), .clr(in_2));  // open: en
  Register #(.width(1)) register_8 (.D(RegWrite_in_2), .Q(RegWrite_out_2), .clk(in_1), .clr(in_2));  // open: en
  Register #(.width(1)) register_9 (.D(MemRead_in_2), .Q(MemRead_out_2), .clk(in_1), .clr(in_2));  // open: en
  Register #(.width(1)) register_10 (.D(MemWrite_in_2), .Q(MemWrite_out_2), .clk(in_1), .clr(in_2));  // open: en
  Register #(.width(1)) register_11 (.D(Branch_in_2), .Q(Branch_out_2), .clk(in_1), .clr(in_2));  // open: en
  Register #(.width(1)) register_12 (.D(Branch_in_3), .Q(Branch_out_3), .clk(in_1), .clr(in_2));  // open: en
  Register #(.width(24)) u_PCinstr (.D(PCinstr), .Q(PCinstr_2), .clk(in_1), .clr(in_2));  // open: en

  // Other names for the same wires on the sheet: clk = in_1; reset = in_2
endmodule

module MemWB (
  input  in_1,
  input  in_2,
  input  [31:0] in_3,
  input  [31:0] in_4,
  input  [4:0] in_5,
  input  [4:0] in_6,
  input  MemToReg_in,
  input  RegWrite_in,
  input  MemRead_in,
  input  RegWrite_in_2,
  input  MemRead_in_2,
  input  MemToReg_in_2,
  input  RegWrite_in_3,
  input  MemRead_in_3,
  input  MemRead_in_4,
  input  [23:0] in_16,
  output [31:0] out_17,
  output [31:0] out_18,
  output [4:0] out_19,
  output [4:0] out_20,
  output MemToReg_out,
  output RegWrite_out,
  output MemRead_out,
  output RegWrite_out_2,
  output MemRead_out_2,
  output MemToReg_out_2,
  output RegWrite_out_3,
  output MemRead_out_3,
  output MemRead_out_4,
  output [23:0] out_30
);

  Register #(.width(32)) register_1 (.D(in_3), .Q(out_17), .clk(in_1), .clr(in_2));  // open: en
  Register #(.width(32)) register_2 (.D(in_4), .Q(out_18), .clk(in_1), .clr(in_2));  // open: en
  Register #(.width(5)) register_3 (.D(in_5), .Q(out_19), .clk(in_1), .clr(in_2));  // open: en
  Register #(.width(5)) register_4 (.D(in_6), .Q(out_20), .clk(in_1), .clr(in_2));  // open: en
  Register #(.width(1)) register_5 (.D(MemToReg_in), .Q(MemToReg_out), .clk(in_1), .clr(in_2));  // open: en
  Register #(.width(1)) register_6 (.D(RegWrite_in), .Q(RegWrite_out), .clk(in_1), .clr(in_2));  // open: en
  Register #(.width(1)) register_7 (.D(MemRead_in), .Q(MemRead_out), .clk(in_1), .clr(in_2));  // open: en
  Register #(.width(1)) register_8 (.D(RegWrite_in_2), .Q(RegWrite_out_2), .clk(in_1), .clr(in_2));  // open: en
  Register #(.width(1)) register_9 (.D(MemRead_in_2), .Q(MemRead_out_2), .clk(in_1), .clr(in_2));  // open: en
  Register #(.width(1)) register_10 (.D(MemToReg_in_2), .Q(MemToReg_out_2), .clk(in_1), .clr(in_2));  // open: en
  Register #(.width(1)) register_11 (.D(RegWrite_in_3), .Q(RegWrite_out_3), .clk(in_1), .clr(in_2));  // open: en
  Register #(.width(1)) register_12 (.D(MemRead_in_3), .Q(MemRead_out_3), .clk(in_1), .clr(in_2));  // open: en
  Register #(.width(1)) register_13 (.D(MemRead_in_4), .Q(MemRead_out_4), .clk(in_1), .clr(in_2));  // open: en
  Register #(.width(24)) register_14 (.D(in_16), .Q(out_30), .clk(in_1), .clr(in_2));  // open: en

  // Other names for the same wires on the sheet: clk = in_1; reset = in_2
endmodule

module ExHazard (
  input  ExMemRegWr,
  input  [4:0] ExMemRd,
  input  [4:0] IDExcRs,
  input  [4:0] IDExcRt,
  output ForwardA,
  output forward,
  output ForwardB
);

  wire comparator_1_eq, comparator_2_eq, comparator_3_eq, not_1_out;

  Comparator #(.width(5)) comparator_1 (.a(ExMemRd), .b({5{1'b0}}), .eq(comparator_1_eq));  // open: gt, lt
  Comparator #(.width(5)) comparator_2 (.a(ExMemRd), .b(IDExcRs), .eq(comparator_2_eq));  // open: gt, lt
  Comparator #(.width(5)) comparator_3 (.a(ExMemRd), .b(IDExcRt), .eq(comparator_3_eq));  // open: gt, lt
  not not_1 (not_1_out, comparator_1_eq);
  and and_1 (ForwardA, ExMemRegWr, not_1_out, comparator_2_eq);
  and and_2 (ForwardB, ExMemRegWr, not_1_out, comparator_3_eq);
  or or_1 (forward, ForwardA, ForwardB);
endmodule

module MemHazard (
  input  MemWbRegWr,
  input  [4:0] MemWbRd,
  input  [4:0] ExMemRd,
  input  [4:0] IdExRs,
  input  [4:0] IdExRt,
  output ForwardA,
  output Forward,
  output ForwardB
);

  wire comparator_1_eq, comparator_2_eq, comparator_3_eq, comparator_4_eq, comparator_5_eq, not_1_out,
       not_2_out, not_3_out;

  not not_1 (not_1_out, comparator_1_eq);
  Comparator #(.width(5)) comparator_1 (.a({5{1'b0}}), .b(MemWbRd), .eq(comparator_1_eq));  // open: gt, lt
  not not_2 (not_2_out, comparator_2_eq);
  Comparator #(.width(5)) comparator_2 (.a(ExMemRd), .b(IdExRs), .eq(comparator_2_eq));  // open: gt, lt
  Comparator #(.width(5)) comparator_3 (.a(MemWbRd), .b(IdExRs), .eq(comparator_3_eq));  // open: gt, lt
  Comparator #(.width(5)) comparator_4 (.a(ExMemRd), .b(IdExRt), .eq(comparator_4_eq));  // open: gt, lt
  not not_3 (not_3_out, comparator_4_eq);
  Comparator #(.width(5)) comparator_5 (.a(MemWbRd), .b(IdExRt), .eq(comparator_5_eq));  // open: gt, lt
  and and_1 (ForwardA, MemWbRegWr, not_1_out, not_2_out, comparator_3_eq);
  and and_2 (ForwardB, MemWbRegWr, not_1_out, not_3_out, comparator_5_eq);
  or or_1 (Forward, ForwardA, ForwardB);
endmodule

module mostrarInst (
  input  ADD,
  input  LOAD,
  input  STORE,
  input  BRANCH,
  input  JUMP,
  input  ADDI,
  output [31:0] out_7,
  output [31:0] out_8,
  output [31:0] out_9,
  output [31:0] out_10,
  output [31:0] out_11
);

  wire [2:0] Slct;

  BitFinder #(.width(7), .\type ("high1")) bitfinder_1 (
    .in({ADDI, JUMP, BRANCH, STORE, LOAD, ADD, 1'b0}), .index(Slct));  // open: found
  Multiplexer #(.select(3), .width(32), .enable("false")) multiplexer_1 (
    .in1(32'h67380000), .in2(32'h8f19c000), .in3(32'h6f98c780), .in4(32'h7798ce90), .in5(32'hfa58b800),
    .in6(32'h67390000), .out(out_7), .sel(Slct));  // open: in0, in7
  Multiplexer #(.select(3), .width(32), .enable("false")) multiplexer_2 (
    .in1(32'h94a40000), .in2(32'h89252000), .in3(32'h82252400), .in4(32'h94a52890), .in5(32'h2255a400),
    .in6(32'h94a50000), .out(out_8), .sel(Slct));  // open: in0, in7
  Multiplexer #(.select(3), .width(32), .enable("false")) multiplexer_3 (
    .in1(32'h94a40000), .in2(32'h89252000), .in3(32'h62254780), .in4(32'hf72528f0), .in5(32'h2252b800),
    .in6(32'h94a50000), .out(out_9), .sel(Slct));  // open: in0, in7
  Multiplexer #(.select(3), .width(32), .enable("false")) multiplexer_4 (
    .in1(32'hf4a40000), .in2(32'h893d2000), .in3(32'h12252400), .in4(32'h953d2890), .in5(32'h2250a000),
    .in6(32'hf4a50000), .out(out_10), .sel(Slct));  // open: in0, in7
  Multiplexer #(.select(3), .width(32), .enable("false")) multiplexer_5 (
    .in1(32'h97bc0000), .in2(32'hef25e000), .in3(32'he2191780), .in4(32'hf4a52e90), .in5(32'he190a000),
    .in6(32'h97bd0000), .out(out_11), .sel(Slct));  // open: in0, in7
endmodule
