// Logisim project CPU_G8 .circ as structural Verilog
module main (
);

  wire add, add2, add3, add4, addi, addi2, addi3, addi4, and_1_out, branch, branch2, branch3, branch4, clk,
       execmem_1_memread_out_2, execmem_1_memtoreg_out_2, execmem_1_memwrite_out_2, execmem_1_regwrite_out_2,
       exhazard_1_forward, hazard, hazardcontrol_1_out_4, idec_exc_1_branch_out, idec_exc_1_memtoreg_out,
       idec_exc_1_memwrite_out, idec_exc_1_regdst_out, idec_exc_1_regwrite_out, IFIDStall, JUMP, jumpp2,
       jumpp3, jumpp4, k_1_r, load, load2, load3, load4, memRead, memwb_1_memtoreg_out_2, not_2_out, Obranch,
       or_1_out, Ozero, register_3_q, regWrWB, reset, stall1, stall2, stall11, store, store2, store3, store4,
       zero;
  wire [1:0] ALUOp, forwardA, forwardB, idec_exc_1_aluop_out;
  wire [3:0] alucontrol_1_out_3, dis_1_dec, dis_1_unit, dis_2_dec, dis_2_unit, dis_3_dec, dis_3_unit,
       dis_4_dec, dis_4_unit, seleAlu, uca_1_out_3;
  wire [4:0] decodificador_1_shamt, execmem_1_out_26, ExMemRd, IdExRs, memwb_1_out_20, multiplexer_8_out,
       Ord, Ort, Orw, rrd, rrs, rrt;
  wire [5:0] funct, OP;
  wire [6:0] UC;
  wire [8:0] uc_1_regdest;
  wire [14:0] erres;
  wire [15:0] bit_extender_6_out, offset;
  wire [23:0] bit_extender_1_out, bit_extender_2_out, bit_extender_7_out, Branchadd, execmem_1_addbranch,
       if_dec_1_out_7, instr1, instr2, instr3, instr4, multiplexer_1_out, multiplexer_2_out, Opc, pc;
  wire [25:0] jump_t;
  wire [31:0] adder_1_out, ALUSUMA, bit_extender_5_out, execmem_1_addbranch_2, idec_exc_1_data1,
       idec_exc_1_data2, idec_exc_1_offset_2, if_dec_1_out_8, memwb_1_out_17, memwb_1_out_18,
       mostrarinst_1_out_8, mostrarinst_1_out_9, mostrarinst_1_out_10, mostrarinst_1_out_11,
       mostrarinst_1_out_12, mostrarinst_2_out_8, mostrarinst_2_out_9, mostrarinst_2_out_10,
       mostrarinst_2_out_11, mostrarinst_2_out_12, mostrarinst_3_out_8, mostrarinst_3_out_9,
       mostrarinst_3_out_10, mostrarinst_3_out_11, mostrarinst_3_out_12, mostrarinst_4_out_8,
       mostrarinst_4_out_9, mostrarinst_4_out_10, mostrarinst_4_out_11, mostrarinst_4_out_12,
       multiplexer_5_out, multiplexer_7_out, NPC, OALUSUMA, OData, OData2, ram_1_data, ram_2_data,
       register_1_q, UnidadRegistros_out_8, UnidadRegistros_out_9;

  Multiplexer #(.width(24)) multiplexer_1 (
    .in0(pc), .in1(execmem_1_addbranch), .out(multiplexer_1_out), .sel(and_1_out));  // open: en
  // Probe on NPC
  and and_1 (and_1_out, Ozero, Obranch);
  Bit_Extender #(.in_width(26), .out_width(24)) bit_extender_1 (.in(jump_t), .out(bit_extender_1_out));
  Register #(.width(32)) register_1 (.D(NPC), .en(IFIDStall), .Q(register_1_q), .clk(clk), .clr(reset));
  Adder #(.width(32)) adder_1 (.a(register_1_q), .b(32'h1), .out(adder_1_out));  // open: cin, cout
  Bit_Extender #(.in_width(32), .out_width(24)) bit_extender_2 (.in(register_1_q), .out(bit_extender_2_out));
  Multiplexer #(.width(24)) multiplexer_2 (
    .in0(multiplexer_1_out), .in1(bit_extender_1_out), .out(multiplexer_2_out), .sel(JUMP));  // open: en
  Bit_Extender #(.in_width(32), .out_width(24)) bit_extender_3 (.in(adder_1_out), .out(pc));
  assign NPC = {{8{1'b0}}, multiplexer_2_out};  // Bit_Extender bit_extender_4
  // Probe on bit_extender_2_out
  Clock clock_1 (.out(clk));
  Button button_1 (.out(reset));
  DotMatrix #(.inputtype("row"), .matrixcols(32), .matrixrows(5)) dotmatrix_1 (
    .row0(mostrarinst_1_out_8), .row1(mostrarinst_1_out_9), .row2(mostrarinst_1_out_10),
    .row3(mostrarinst_1_out_11), .row4(mostrarinst_1_out_12));
  mostrarInst mostrarinst_1 (
    .ADD(add), .ADDI(addi), .STALL(1'b0), .BRANCH(branch), .JUMP(JUMP), .LOAD(load), .STORE(store),
    .out_8(mostrarinst_1_out_8), .out_9(mostrarinst_1_out_9), .out_10(mostrarinst_1_out_10),
    .out_11(mostrarinst_1_out_11), .out_12(mostrarinst_1_out_12));
  DIS dis_1 (.CONST(1'b1), .PC(instr1), .DEC(dis_1_dec), .UNIT(dis_1_unit));
  IF_Dec if_dec_1 (
    .in_1(clk), .in_2(reset), .Instr(ram_1_data), .out_8(if_dec_1_out_8), .Pc_1(pc), .out_7(if_dec_1_out_7),
    .Pc_instr(bit_extender_2_out), .out_9(instr1), .in_3(IFIDStall));
  RAM #(.addrWidth(24), .dataWidth(32)) ram_1 (
    .addr(bit_extender_2_out), .data(ram_1_data));  // open: sel, clk, ld, clr
  Multiplexer #(.width(15)) multiplexer_3 (
    .in0({15{1'b0}}), .in1({rrs, rrt, rrd}), .out(erres), .sel(IFIDStall));  // open: en
  Hex_Digit_Display hex_digit_display_1 (.value(dis_1_unit));  // open: dp
  Hex_Digit_Display hex_digit_display_2 (.value(dis_1_dec));  // open: dp
  // Probe on funct
  decodificador decodificador_1 (
    .in_1(if_dec_1_out_8), .Funct(funct), .Shamt(decodificador_1_shamt), .RD(rrd), .RT(rrt), .RS(rrs),
    .out_7(OP), .out_8(offset), .out_9(jump_t));
  // Probe on OP
  // Probe on jump_t
  IDhazard idhazard_1 (.IDEXMemRead(memRead), .IDEXRt(Ort), .IFIDRs(rrs), .IFIDRt(rrt), .stall(stall1));
  // Probe on uca_1_out_3
  UCA uca_1 (.ALUOp(ALUOp), .Func(funct), .out_3(uca_1_out_3));
  // Probe on decodificador_1_shamt
  // Probe on rrd
  // Probe on rrt
  // Probe on rrs
  // Probe on offset
  // Probe on instr1
  not not_1 (IFIDStall, stall1);
  Multiplexer #(.width(9)) multiplexer_4 (
    .in0({9{1'b0}}), .in1(uc_1_regdest), .out({ALUOp, UC[6:2], addi, UC[0]}), .sel(IFIDStall));  // open: en
  k k_1 (.in_1(OP), .r(k_1_r), .Add(add), .load(load), .store(store), .branch(branch), .jump(JUMP));
  LED R (.in(k_1_r));
  LED u_ADD (.in(add));
  LED u_LOAD (.in(load));
  LED u_STORE (.in(store));
  LED u_BRANCH (.in(branch));
  LED JUMP_2 (.in(JUMP));
  not not_2 (not_2_out, clk);
  UC uc_1 (
    .in_1(OP), .RegDest(uc_1_regdest[0]), .ALUsrc(uc_1_regdest[1]), .MemtoReg(uc_1_regdest[2]),
    .RegWrite(uc_1_regdest[3]), .MemRead(uc_1_regdest[4]), .MemWrite(uc_1_regdest[5]),
    .Branch(uc_1_regdest[6]), .out_9(uc_1_regdest[8:7]));
  UnidadRegistros UnidadRegistros (
    .rs(erres[14:10]), .rt(erres[9:5]), .rw(Orw), .in_4(OData), .in_5(not_2_out), .in_6(reset),
    .out_8(UnidadRegistros_out_8), .out_9(UnidadRegistros_out_9), .regWrite(regWrWB));
  ALUcontrol alucontrol_1 (.ALUOp(ALUOp), .funct(funct), .out_3(alucontrol_1_out_3));
  mostrarInst mostrarinst_2 (
    .ADD(add2), .ADDI(addi2), .STALL(stall11), .BRANCH(branch2), .JUMP(jumpp2), .LOAD(load2), .STORE(store2),
    .out_8(mostrarinst_2_out_8), .out_9(mostrarinst_2_out_9), .out_10(mostrarinst_2_out_10),
    .out_11(mostrarinst_2_out_11), .out_12(mostrarinst_2_out_12));
  DotMatrix #(.inputtype("row"), .matrixcols(32), .matrixrows(5)) dotmatrix_2 (
    .row0(mostrarinst_2_out_8), .row1(mostrarinst_2_out_9), .row2(mostrarinst_2_out_10),
    .row3(mostrarinst_2_out_11), .row4(mostrarinst_2_out_12));
  DIS dis_2 (.CONST(1'b1), .PC(instr2), .DEC(dis_2_dec), .UNIT(dis_2_unit));
  IDec_Exc idec_exc_1 (
    .in_1(clk), .in_2(reset), .Pc_1(if_dec_1_out_7), .pc_1_2(Opc), .Data1RS(UnidadRegistros_out_8),
    .Data1(idec_exc_1_data1), .Data2RT(UnidadRegistros_out_9), .Data2(idec_exc_1_data2),
    .offset(bit_extender_5_out), .offset_2(idec_exc_1_offset_2), .Pc_instr(instr1), .out_47(instr2),
    .in_8(erres[9:5]), .in_9(erres[4:0]), .out_31(Ort), .out_32(Ord), .RegDst_in(UC[0]),
    .RegDst_out(idec_exc_1_regdst_out), .ALUsrc_in(addi), .ALUsrc_out(addi2), .MemToReg_in(UC[2]),
    .MemToReg_out(idec_exc_1_memtoreg_out), .RegWrite_in(UC[3]), .RegWrite_out(idec_exc_1_regwrite_out),
    .MemRead_in(UC[4]), .MemRead_out(memRead), .MemWrite_in(UC[5]), .MemWrite_out(idec_exc_1_memwrite_out),
    .Branch_in(UC[6]), .Branch_out(idec_exc_1_branch_out), .ALUOp_in(ALUOp),
    .ALUOp_out(idec_exc_1_aluop_out), .rs(erres[14:10]), .rs_2(IdExRs), .RegDst_in_2(add),
    .RegDst_out_2(add2), .ALUsrc_in_2(load), .ALUsrc_out_2(load2), .MemToReg_in_2(store),
    .MemToReg_out_2(store2), .RegWrite_in_2(branch), .RegWrite_out_2(branch2), .MemRead_in_2(JUMP),
    .MemRead_out_2(jumpp2), .in_3(1'b1), .in_25(alucontrol_1_out_3), .out_48(seleAlu), .in_11(stall1),
    .out_34(stall11));
  assign bit_extender_5_out = {{16{1'b0}}, offset};  // Bit_Extender bit_extender_5
  Hex_Digit_Display hex_digit_display_3 (.value(dis_2_dec));  // open: dp
  Hex_Digit_Display hex_digit_display_4 (.value(dis_2_unit));  // open: dp
  Multiplexer #(.select(2), .width(32)) multiplexer_5 (
    .in0(idec_exc_1_data1), .in1(OData), .in2(OALUSUMA), .out(multiplexer_5_out), .sel(forwardA));  // open: in3, en
  // Probe on forwardA
  Multiplexer #(.select(2), .width(32)) multiplexer_6 (
    .in0(idec_exc_1_data2), .in1(OData), .in2(OALUSUMA), .out(OData2), .sel(forwardB));  // open: in3, en
  // Probe on forwardB
  // Probe on instr2
  Multiplexer #(.width(32)) multiplexer_7 (
    .in0(OData2), .in1(idec_exc_1_offset_2), .out(multiplexer_7_out), .sel(addi2));  // open: en
  branch branch_2 (.offset(bit_extender_6_out), .out_3(Branchadd), .pc(Opc));
  Bit_Extender #(.in_width(32)) bit_extender_6 (.in(idec_exc_1_offset_2), .out(bit_extender_6_out));
  Register #(.width(1)) register_2 (.D(stall11), .Q(stall2), .clk(clk), .clr(reset));  // open: en
  ALU alu_1 (.DATA1(multiplexer_5_out), .DATA2(multiplexer_7_out), .AluControl(seleAlu), .RESULT(ALUSUMA), .Zero(zero));
  // Probe on ALUSUMA
  Multiplexer #(.width(5)) multiplexer_8 (.in0(Ord), .in1(Ort), .out(multiplexer_8_out), .sel(addi2));  // open: en
  ExecMem execmem_1 (
    .in_4(Branchadd), .AddBranch(execmem_1_addbranch), .zero(zero), .Ozero(Ozero), .ALUSUMA(ALUSUMA),
    .OALUSUMA(OALUSUMA), .in_7(OData2), .AddBranch_2(execmem_1_addbranch_2), .PCinstr(instr2),
    .PCinstr_2(instr3), .in_1(clk), .in_2(reset), .in_8(multiplexer_8_out), .out_26(execmem_1_out_26),
    .MemToReg_in_2(idec_exc_1_memtoreg_out), .MemToReg_out_2(execmem_1_memtoreg_out_2),
    .RegWrite_in_2(idec_exc_1_regwrite_out), .RegWrite_out_2(execmem_1_regwrite_out_2),
    .MemRead_in_2(memRead), .MemRead_out_2(execmem_1_memread_out_2), .MemWrite_in_2(idec_exc_1_memwrite_out),
    .MemWrite_out_2(execmem_1_memwrite_out_2), .Branch_in_2(idec_exc_1_branch_out), .Branch_out_2(Obranch),
    .rd(Ord), .rd_2(ExMemRd), .MemToReg_in(add2), .MemToReg_out(add3), .RegWrite_in(load2),
    .RegWrite_out(load3), .MemRead_in(store2), .MemRead_out(store3), .MemWrite_in(branch2),
    .MemWrite_out(branch3), .Branch_in(jumpp2), .Branch_out(jumpp3), .Branch_in_3(addi2),
    .Branch_out_3(addi3), .in_3(1'b1));
  mostrarInst mostrarinst_3 (
    .ADD(add3), .ADDI(addi3), .STALL(stall2), .BRANCH(branch3), .JUMP(jumpp3), .LOAD(load3), .STORE(store3),
    .out_8(mostrarinst_3_out_8), .out_9(mostrarinst_3_out_9), .out_10(mostrarinst_3_out_10),
    .out_11(mostrarinst_3_out_11), .out_12(mostrarinst_3_out_12));
  DotMatrix #(.inputtype("row"), .matrixcols(32), .matrixrows(5)) dotmatrix_3 (
    .row0(mostrarinst_3_out_8), .row1(mostrarinst_3_out_9), .row2(mostrarinst_3_out_10),
    .row3(mostrarinst_3_out_11), .row4(mostrarinst_3_out_12));
  DIS dis_3 (.CONST(1'b1), .PC(instr3), .DEC(dis_3_dec), .UNIT(dis_3_unit));
  Hex_Digit_Display hex_digit_display_5 (.value(dis_3_unit));  // open: dp
  Hex_Digit_Display hex_digit_display_6 (.value(dis_3_dec));  // open: dp
  Bit_Extender #(.in_width(32), .out_width(24)) bit_extender_7 (.in(OALUSUMA), .out(bit_extender_7_out));
  // Probe on instr3
  not not_3 (hazard, exhazard_1_forward);
  LED Forward (.in(exhazard_1_forward));
  ExHazard exhazard_1 (
    .ExMemRegWr(execmem_1_regwrite_out_2), .ExMemRd(execmem_1_out_26), .IDExcRs(IdExRs), .IDExcRt(Ort),
    .forward(exhazard_1_forward), .ForwardA(forwardA), .ForwardB(forwardB), .MemWbRegWr(regWrWB),
    .MemWbRd(Orw));
  or or_1 (or_1_out, execmem_1_memwrite_out_2, execmem_1_memread_out_2);
  Register #(.width(1)) register_3 (.D(stall2), .Q(register_3_q), .clk(clk), .clr(reset));  // open: en
  RAM #(.addrWidth(24), .dataWidth(32), .bus("separate")) ram_2 (
    .addr(bit_extender_7_out), .din(execmem_1_addbranch_2), .data(ram_2_data), .sel(or_1_out), .clk(clk),
    .ld(execmem_1_memread_out_2), .clr(reset));  // open: str
  HazardControl hazardcontrol_1 (
    .pc_ExcMem(instr3), .pc_Memwb(instr4), .Hazard(hazard), .out_4(hazardcontrol_1_out_4));  // open: enable
  MemWB memwb_1 (
    .in_4(OALUSUMA), .out_18(memwb_1_out_18), .in_3(ram_2_data), .out_17(memwb_1_out_17), .in_16(instr3),
    .out_30(instr4), .in_1(clk), .in_2(reset), .in_5(execmem_1_out_26), .out_19(Orw),
    .MemToReg_in_2(execmem_1_memtoreg_out_2), .MemToReg_out_2(memwb_1_memtoreg_out_2),
    .RegWrite_in_3(execmem_1_regwrite_out_2), .RegWrite_out_3(regWrWB),
    .MemRead_in_3(execmem_1_memread_out_2), .in_6(ExMemRd), .out_20(memwb_1_out_20), .MemToReg_in(add3),
    .MemToReg_out(add4), .RegWrite_in(load3), .RegWrite_out(load4), .MemRead_in(store3),
    .MemRead_out(store4), .RegWrite_in_2(branch3), .RegWrite_out_2(branch4), .MemRead_in_2(jumpp3),
    .MemRead_out_2(jumpp4), .MemRead_in_4(addi3), .MemRead_out_4(addi4));  // open: MemRead_out_3
  DotMatrix #(.inputtype("row"), .matrixcols(32), .matrixrows(5)) dotmatrix_4 (
    .row0(mostrarinst_4_out_8), .row1(mostrarinst_4_out_9), .row2(mostrarinst_4_out_10),
    .row3(mostrarinst_4_out_11), .row4(mostrarinst_4_out_12));
  mostrarInst mostrarinst_4 (
    .ADD(add4), .ADDI(addi4), .STALL(register_3_q), .BRANCH(branch4), .JUMP(jumpp4), .LOAD(load4),
    .STORE(store4), .out_8(mostrarinst_4_out_8), .out_9(mostrarinst_4_out_9), .out_10(mostrarinst_4_out_10),
    .out_11(mostrarinst_4_out_11), .out_12(mostrarinst_4_out_12));
  DIS dis_4 (.CONST(1'b1), .PC(instr4), .DEC(dis_4_dec), .UNIT(dis_4_unit));
  // Probe on instr4
  Hex_Digit_Display hex_digit_display_7 (.value(dis_4_dec));  // open: dp
  Multiplexer #(.width(32)) multiplexer_9 (
    .in0(memwb_1_out_18), .in1(memwb_1_out_17), .out(OData), .sel(memwb_1_memtoreg_out_2));  // open: en
  Hex_Digit_Display hex_digit_display_8 (.value(dis_4_unit));  // open: dp

  // Other names for the same wires on the sheet: rd[4:0] = erres[4:0]; rt[4:0] = erres[9:5]; rs[4:0] = erres[14:10];
  //   jumpp = JUMP; pcinst3[23:0] = instr3; UC (some bits) = {ALUOp, addi}

  // Notes on the sheet:
  //   IF-Dec
  //   Funct
  //   Shamt
  //   Rd
  //   Rt
  //   RS
  //   OP
  //   Offset
  //   RegDest
  //   ALUsrc
  //   MToReg
  //   RegWr
  //   MemRead
  //   MemWR
  //   Branch
  //   ALUOp
  //   Data1
  //   Data 2
  //   Offset
  //   IDec-Exc
  //   ALUsrc
  //   BranchAdd
  //   BranchAdd
  //   ALUSUMA
  //   Data2
  //   RW
  //   ExcMem
  //   MemWR
  //   ReadData
  //   ReadData
  //   ALUSUMA
  //   MemWB
  //   MToReg
endmodule

module ALU (
  input  [31:0] DATA1,
  input  [31:0] DATA2,
  input  [3:0] AluControl,
  output [31:0] RESULT,
  output Zero
);

  wire comparator_1_eq, comparator_2_eq, comparator_3_eq, comparator_4_eq;
  wire [2:0] priority_encoder_1_out;
  wire [31:0] add, \and , \or , Sub;

  Comparator #(.width(4)) comparator_1 (.a(AluControl), .b(4'b0010), .eq(comparator_1_eq));  // open: gt, lt
  Comparator #(.width(4)) comparator_2 (.a(AluControl), .b(4'b0110), .eq(comparator_2_eq));  // open: gt, lt
  Comparator #(.width(4)) comparator_3 (.a(AluControl), .b(4'b0000), .eq(comparator_3_eq));  // open: gt, lt
  Comparator #(.width(4)) comparator_4 (.a(AluControl), .b(4'b0001), .eq(comparator_4_eq));  // open: gt, lt
  Adder #(.width(32)) adder_1 (.a(DATA1), .b(DATA2), .out(add));  // open: cin, cout
  Subtractor #(.width(32)) subtractor_1 (.a(DATA1), .b(DATA2), .out(Sub));  // open: bin, bout
  Comparator #(.width(32)) comparator_5 (.a(DATA1), .b(DATA2), .eq(Zero));  // open: gt, lt
  Priority_Encoder priority_encoder_1 (
    .in0(comparator_1_eq), .in1(comparator_2_eq), .in2(comparator_3_eq), .in3(comparator_4_eq),
    .out(priority_encoder_1_out));  // open: in4, in5, in6, in7, en_in, gs, en_out
  assign \and  = DATA1 & DATA2;  // AND_Gate and_1, 32 bits wide
  assign \or  = DATA1 | DATA2;  // OR_Gate or_1, 32 bits wide
  Multiplexer #(.select(3), .width(32), .enable("false")) multiplexer_1 (
    .in0(add), .in1(Sub), .in2(\and ), .in3(\or ), .out(RESULT), .sel(priority_encoder_1_out));  // open: in4, in5, in6, in7

  // Other names for the same wires on the sheet: A[31:0] = DATA1; B[31:0] = DATA2

  // Notes on the sheet:
  //   Add
  //   0010
  //   Substract
  //   0110
  //   and
  //   0000
  //   or
  //   0001
endmodule

// ALUC
module ALUcontrol (
  input  [1:0] ALUOp,
  input  [5:0] funct,
  output [3:0] out_3
);

  wire and_1_out, and_2_out, and_3_out, and_4_out, and_5_out, and_6_out, not_1_out, not_2_out, not_3_out,
       not_4_out, not_5_out, not_6_out, not_7_out, not_8_out;

  not not_1 (not_1_out, ALUOp[1]);
  not not_2 (not_2_out, funct[2]);
  not not_3 (not_3_out, ALUOp[1]);
  not not_4 (not_4_out, funct[2]);
  not not_5 (not_5_out, funct[3]);
  not not_6 (not_6_out, funct[1]);
  not not_7 (not_7_out, funct[2]);
  not not_8 (not_8_out, funct[0]);
  and and_1 (and_1_out, not_1_out, ALUOp[0]);
  and and_2 (and_2_out, ALUOp[1], not_2_out, funct[0]);
  and and_3 (and_3_out, ALUOp[1], funct[1]);
  and and_4 (and_4_out, ALUOp[1], funct[3]);
  or or_1 (out_3[1], not_3_out, not_4_out, funct[1], funct[3]);
  and and_5 (and_5_out, ALUOp[1], not_5_out, funct[2], not_6_out, funct[0]);
  and and_6 (and_6_out, ALUOp[1], funct[3], not_7_out, funct[1], not_8_out);
  or or_2 (out_3[2], and_1_out, and_2_out, and_3_out, and_4_out);
  or or_3 (out_3[0], and_5_out, and_6_out);

  assign out_3[3] = 1'b0;
endmodule

// Spliter
module decodificador (
  input  [31:0] in_1,
  output [5:0] Funct,
  output [4:0] Shamt,
  output [4:0] RD,
  output [4:0] RT,
  output [4:0] RS,
  output [5:0] out_7,
  output [15:0] out_8,
  output [25:0] out_9
);


  assign Funct = in_1[5:0];
  assign out_7 = in_1[31:26];
  assign out_8 = in_1[15:0];
  assign out_9 = in_1[25:0];
  assign RD = in_1[15:11];
  assign RS = in_1[25:21];
  assign RT = in_1[20:16];
  assign Shamt = in_1[10:6];

  // Notes on the sheet:
  //   R
  //   Branch
  //   Jump
  //   OP Code
  //   Offset
  //   Jump
endmodule

module k (
  input  [5:0] in_1,
  output r,
  output Add,
  output load,
  output store,
  output branch,
  output jump
);

  Comparator #(.width(6)) comparator_1 (.a(in_1), .b({6{1'b0}}), .eq(r));  // open: gt, lt
  Comparator #(.width(6)) comparator_2 (.a(in_1), .b({6{1'b0}}), .eq(Add));  // open: gt, lt
  Comparator #(.width(6)) comparator_3 (.a(in_1), .b(6'b100011), .eq(load));  // open: gt, lt
  Comparator #(.width(6)) comparator_4 (.a(in_1), .b(6'b101011), .eq(store));  // open: gt, lt
  Comparator #(.width(6)) comparator_5 (.a(in_1), .b(6'b000100), .eq(branch));  // open: gt, lt
  Comparator #(.width(6)) comparator_6 (.a(in_1), .b(6'b000010), .eq(jump));  // open: gt, lt
endmodule

// UR
module UnidadRegistros (
  input  [4:0] rs,
  input  [4:0] rt,
  input  [4:0] rw,
  input  [31:0] in_4,
  input  in_5,
  input  in_6,
  input  regWrite,
  output [31:0] out_8,
  output [31:0] out_9
);

  wire B0, B1, B2, B3, B4, B5, B6, B7, B8, B9, B10, B11, B12, B13, B14, B15, B16, B17, B18, B19, B20, B21,
       B22, B23, B24, B25, B26, B27, B28, B29, B30, B31;
  wire [31:0] _0, _1, _2, _3, _4, _5, _6, _7, _8, _9, _10, _11, _12, _13, _14, _15, _16, _17, _18, _19, _20,
       _21, _22, _23, _24, _25, _26, _27, _28, _29, _30, _31, r0, r1, r2, r3, r4, r5, r6, r7, r8, r9, r10,
       r11, r12, r13, r14, r15, r16, r17, r18, r19, r20, r21, r22, r23, r24, r25, r26, r27, r28, r29, r30,
       r31;

  Register #(.width(32)) register_1 (.D(_0), .en(B0), .Q(r0), .clk(in_5), .clr(in_6));
  Register #(.width(32)) register_2 (.D(_1), .en(B1), .Q(r1), .clk(in_5), .clr(in_6));
  Register #(.width(32)) register_3 (.D(_2), .en(B2), .Q(r2), .clk(in_5), .clr(in_6));
  Register #(.width(32)) register_4 (.D(_3), .en(B3), .Q(r3), .clk(in_5), .clr(in_6));
  Register #(.width(32)) register_5 (.D(_4), .en(B4), .Q(r4), .clk(in_5), .clr(in_6));
  Register #(.width(32)) register_6 (.D(_5), .en(B5), .Q(r5), .clk(in_5), .clr(in_6));
  Register #(.width(32)) register_7 (.D(_6), .en(B6), .Q(r6), .clk(in_5), .clr(in_6));
  Register #(.width(32)) register_8 (.D(_7), .en(B7), .Q(r7), .clk(in_5), .clr(in_6));
  Register #(.width(32)) register_9 (.D(_8), .en(B8), .Q(r8), .clk(in_5), .clr(in_6));
  Register #(.width(32)) register_10 (.D(_9), .en(B9), .Q(r9), .clk(in_5), .clr(in_6));
  Register #(.width(32)) register_11 (.D(_10), .en(B10), .Q(r10), .clk(in_5), .clr(in_6));
  Register #(.width(32)) register_12 (.D(_11), .en(B11), .Q(r11), .clk(in_5), .clr(in_6));
  Register #(.width(32)) register_13 (.D(_12), .en(B12), .Q(r12), .clk(in_5), .clr(in_6));
  Register #(.width(32)) register_14 (.D(_13), .en(B13), .Q(r13), .clk(in_5), .clr(in_6));
  Register #(.width(32)) register_15 (.D(_14), .en(B14), .Q(r14), .clk(in_5), .clr(in_6));
  Register #(.width(32)) register_16 (.D(_15), .en(B15), .Q(r15), .clk(in_5), .clr(in_6));
  // Probe on nothing
  Register #(.width(32)) register_17 (.D(_16), .en(B16), .Q(r16), .clk(in_5), .clr(in_6));
  Register #(.width(32)) register_18 (.D(_17), .en(B17), .Q(r17), .clk(in_5), .clr(in_6));
  Register #(.width(32)) register_19 (.D(_18), .en(B18), .Q(r18), .clk(in_5), .clr(in_6));
  Register #(.width(32)) register_20 (.D(_19), .en(B19), .Q(r19), .clk(in_5), .clr(in_6));
  Register #(.width(32)) register_21 (.D(_20), .en(B20), .Q(r20), .clk(in_5), .clr(in_6));
  Register #(.width(32)) register_22 (.D(_21), .en(B21), .Q(r21), .clk(in_5), .clr(in_6));
  Register #(.width(32)) register_23 (.D(_22), .en(B22), .Q(r22), .clk(in_5), .clr(in_6));
  Register #(.width(32)) register_24 (.D(_23), .en(B23), .Q(r23), .clk(in_5), .clr(in_6));
  Register #(.width(32)) register_25 (.D(_24), .en(B24), .Q(r24), .clk(in_5), .clr(in_6));
  Register #(.width(32)) register_26 (.D(_25), .en(B25), .Q(r25), .clk(in_5), .clr(in_6));
  Register #(.width(32)) register_27 (.D(_26), .en(B26), .Q(r26), .clk(in_5), .clr(in_6));
  Register #(.width(32)) register_28 (.D(_27), .en(B27), .Q(r27), .clk(in_5), .clr(in_6));
  Register #(.width(32)) register_29 (.D(_28), .en(B28), .Q(r28), .clk(in_5), .clr(in_6));
  Register #(.width(32)) register_30 (.D(_29), .en(B29), .Q(r29), .clk(in_5), .clr(in_6));
  Register #(.width(32)) register_31 (.D(_30), .en(B30), .Q(r30), .clk(in_5), .clr(in_6));
  Register #(.width(32)) register_32 (.D(_31), .en(B31), .Q(r31), .clk(in_5), .clr(in_6));
  Multiplexer #(.select(5), .width(32)) multiplexer_1 (
    .in0(r0), .in1(r1), .in2(r2), .in3(r3), .in4(r4), .in5(r5), .in6(r6), .in7(r7), .in8(r8), .in9(r9),
    .in10(r10), .in11(r11), .in12(r12), .in13(r13), .in14(r14), .in15(r15), .in16(r16), .in17(r17),
    .in18(r18), .in19(r19), .in20(r20), .in21(r21), .in22(r22), .in23(r23), .in24(r24), .in25(r25),
    .in26(r26), .in27(r27), .in28(r28), .in29(r29), .in30(r30), .in31(r31), .out(out_8), .sel(rs));  // open: en
  Multiplexer #(.select(5), .width(32)) multiplexer_2 (
    .in0(r0), .in1(r1), .in2(r2), .in3(r3), .in4(r4), .in5(r5), .in6(r6), .in7(r7), .in8(r8), .in9(r9),
    .in10(r10), .in11(r11), .in12(r12), .in13(r13), .in14(r14), .in15(r15), .in16(r16), .in17(r17),
    .in18(r18), .in19(r19), .in20(r20), .in21(r21), .in22(r22), .in23(r23), .in24(r24), .in25(r25),
    .in26(r26), .in27(r27), .in28(r28), .in29(r29), .in30(r30), .in31(r31), .out(out_9), .sel(rt));  // open: en
  Demultiplexer #(.select(5)) demultiplexer_1 (
    .out0(B0), .out1(B1), .out2(B2), .out3(B3), .out4(B4), .out5(B5), .out6(B6), .out7(B7), .out8(B8),
    .out9(B9), .out10(B10), .out11(B11), .out12(B12), .out13(B13), .out14(B14), .out15(B15), .out16(B16),
    .out17(B17), .out18(B18), .out19(B19), .out20(B20), .out21(B21), .out22(B22), .out23(B23), .out24(B24),
    .out25(B25), .out26(B26), .out27(B27), .out28(B28), .out29(B29), .out30(B30), .out31(B31), .in(regWrite),
    .sel(rw));  // open: en
  Demultiplexer #(.select(5), .width(32)) demultiplexer_2 (
    .out0(_0), .out1(_1), .out2(_2), .out3(_3), .out4(_4), .out5(_5), .out6(_6), .out7(_7), .out8(_8),
    .out9(_9), .out10(_10), .out11(_11), .out12(_12), .out13(_13), .out14(_14), .out15(_15), .out16(_16),
    .out17(_17), .out18(_18), .out19(_19), .out20(_20), .out21(_21), .out22(_22), .out23(_23), .out24(_24),
    .out25(_25), .out26(_26), .out27(_27), .out28(_28), .out29(_29), .out30(_30), .out31(_31), .in(in_4),
    .sel(rw));  // open: en

  // Other names for the same wires on the sheet: clk = in_5; Data[31:0] = in_4; reset = in_6
endmodule

module UC (
  input  [5:0] in_1,
  output RegDest,
  output ALUsrc,
  output MemtoReg,
  output RegWrite,
  output MemRead,
  output MemWrite,
  output Branch,
  output [1:0] out_9
);

  wire and_5_out, and_6_out, not_2_out, not_3_out, not_4_out, not_5_out, not_6_out;

  not not_1 (RegDest, in_1[5]);
  or or_1 (ALUsrc, in_1[1], in_1[3]);
  not not_2 (not_2_out, in_1[2]);
  not not_3 (not_3_out, in_1[3]);
  not not_4 (not_4_out, in_1[2]);
  not not_5 (not_5_out, in_1[5]);
  and and_1 (MemRead, in_1[1], not_6_out);
  not not_6 (not_6_out, in_1[3]);
  and and_2 (MemWrite, in_1[3], in_1[0]);
  and and_3 (out_9[1], ~in_1[5], ~in_1[4], ~in_1[3], ~in_1[2], ~in_1[1], ~in_1[0]);  // AND_Gate
  and and_4 (out_9[0], ~in_1[5], ~in_1[4], ~in_1[3], in_1[2], ~in_1[1], ~in_1[0]);  // AND_Gate
  and and_5 (and_5_out, not_2_out, not_3_out);
  and and_6 (and_6_out, not_4_out, not_5_out);
  or or_2 (RegWrite, and_5_out, and_6_out);

  assign Branch = in_1[2];
  assign MemtoReg = in_1[1];
endmodule

module UCA (
  input  [1:0] ALUOp,
  input  [5:0] Func,
  output [3:0] out_3
);

  wire and_1_out, and_2_out, and_3_out, and_4_out, not_1_out, not_2_out, not_3_out;

  not not_1 (not_1_out, ALUOp[0]);
  not not_2 (not_2_out, ALUOp[0]);
  not not_3 (not_3_out, Func[2]);
  and and_1 (and_1_out, ALUOp[0], Func[0]);
  and and_2 (and_2_out, ALUOp[0], Func[3]);
  and and_3 (and_3_out, not_1_out, ALUOp[1]);
  and and_4 (and_4_out, ALUOp[0], Func[1]);
  or or_1 (out_3[1], not_2_out, not_3_out);
  or or_2 (out_3[0], and_1_out, and_2_out);
  or or_3 (out_3[2], and_3_out, and_4_out);

  assign out_3[3] = 1'b0;
endmodule

// Branch
module branch (
  input  [23:0] pc,
  input  [15:0] offset,
  output [23:0] out_3
);

  wire [23:0] adder_1_out, bit_extender_1_out, subtractor_1_out;

  assign bit_extender_1_out = {{9{1'b0}}, offset[14:0]};  // Bit_Extender bit_extender_1
  Adder #(.width(24)) adder_1 (.a(pc), .b(bit_extender_1_out), .out(adder_1_out));  // open: cin, cout
  Subtractor #(.width(24)) subtractor_1 (.a(pc), .b(bit_extender_1_out), .out(subtractor_1_out));  // open: bin, bout
  Multiplexer #(.width(24)) multiplexer_1 (
    .in0(adder_1_out), .in1(subtractor_1_out), .out(out_3), .sel(offset[15]));  // open: en
endmodule

module IF_Dec (
  input  in_1,
  input  in_2,
  input  in_3,
  input  [23:0] Pc_1,
  input  [31:0] Instr,
  input  [23:0] Pc_instr,
  output [23:0] out_7,
  output [31:0] out_8,
  output [23:0] out_9
);

  Register #(.width(24)) u_PC_1 (.D(Pc_1), .en(in_3), .Q(out_7), .clk(in_1), .clr(in_2));
  Register #(.width(32)) u_Instr (.D(Instr), .en(in_3), .Q(out_8), .clk(in_1), .clr(in_2));
  Register #(.width(24)) PC_Ins (.D(Pc_instr), .en(in_3), .Q(out_9), .clk(in_1), .clr(in_2));

  // Other names for the same wires on the sheet: clk = in_1; reset = in_2; stall = in_3
endmodule

module IDec_Exc (
  input  in_1,
  input  in_2,
  input  in_3,
  input  [23:0] Pc_1,
  input  [31:0] Data1RS,
  input  [31:0] Data2RT,
  input  [31:0] offset,
  input  [4:0] in_8,
  input  [4:0] in_9,
  input  [4:0] rs,
  input  in_11,
  input  RegDst_in,
  input  RegDst_in_2,
  input  ALUsrc_in,
  input  ALUsrc_in_2,
  input  MemToReg_in,
  input  MemToReg_in_2,
  input  RegWrite_in,
  input  RegWrite_in_2,
  input  MemRead_in,
  input  MemRead_in_2,
  input  MemWrite_in,
  input  Branch_in,
  input  [23:0] Pc_instr,
  input  [3:0] in_25,
  input  [1:0] ALUOp_in,
  output [23:0] pc_1_2,
  output [31:0] Data1,
  output [31:0] Data2,
  output [31:0] offset_2,
  output [4:0] out_31,
  output [4:0] out_32,
  output [4:0] rs_2,
  output out_34,
  output RegDst_out,
  output RegDst_out_2,
  output ALUsrc_out,
  output ALUsrc_out_2,
  output MemToReg_out,
  output MemToReg_out_2,
  output RegWrite_out,
  output RegWrite_out_2,
  output MemRead_out,
  output MemRead_out_2,
  output MemWrite_out,
  output Branch_out,
  output [23:0] out_47,
  output [3:0] out_48,
  output [1:0] ALUOp_out
);

  Register #(.width(24)) u_PC_1 (.D(Pc_1), .en(in_3), .Q(pc_1_2), .clk(in_1), .clr(in_2));
  Register #(.width(32)) dataRS (.D(Data1RS), .en(in_3), .Q(Data1), .clk(in_1), .clr(in_2));
  Register #(.width(32)) dataRT (.D(Data2RT), .en(in_3), .Q(Data2), .clk(in_1), .clr(in_2));
  Register #(.width(32)) u_offset (.D(offset), .en(in_3), .Q(offset_2), .clk(in_1), .clr(in_2));
  Register #(.width(5)) register_1 (.D(in_8), .en(in_3), .Q(out_31), .clk(in_1), .clr(in_2));
  Register #(.width(5)) register_2 (.D(in_9), .en(in_3), .Q(out_32), .clk(in_1), .clr(in_2));
  Register #(.width(5)) u_rs (.D(rs), .en(in_3), .Q(rs_2), .clk(in_1), .clr(in_2));
  Register #(.width(1)) register_3 (.D(in_11), .Q(out_34), .clk(in_1), .clr(in_2));  // open: en
  Register #(.width(1)) register_4 (.D(RegDst_in), .en(in_3), .Q(RegDst_out), .clk(in_1), .clr(in_2));
  Register #(.width(1)) register_5 (.D(ALUsrc_in), .en(in_3), .Q(ALUsrc_out), .clk(in_1), .clr(in_2));
  Register #(.width(1)) register_6 (.D(MemToReg_in), .en(in_3), .Q(MemToReg_out), .clk(in_1), .clr(in_2));
  Register #(.width(1)) register_7 (.D(RegWrite_in), .en(in_3), .Q(RegWrite_out), .clk(in_1), .clr(in_2));
  Register #(.width(1)) register_8 (.D(MemRead_in), .en(in_3), .Q(MemRead_out), .clk(in_1), .clr(in_2));
  Register #(.width(1)) register_9 (.D(MemWrite_in), .en(in_3), .Q(MemWrite_out), .clk(in_1), .clr(in_2));
  Register #(.width(1)) register_10 (.D(Branch_in), .en(in_3), .Q(Branch_out), .clk(in_1), .clr(in_2));
  Register #(.width(24)) PC_Ins (.D(Pc_instr), .en(in_3), .Q(out_47), .clk(in_1), .clr(in_2));
  Register #(.width(4)) PC_Ins_2 (.D(in_25), .Q(out_48), .clk(in_1), .clr(in_2));  // open: en
  Register #(.width(2)) register_11 (.D(ALUOp_in), .en(in_3), .Q(ALUOp_out), .clk(in_1), .clr(in_2));
  Register #(.width(1)) register_12 (.D(RegDst_in_2), .en(in_3), .Q(RegDst_out_2), .clk(in_1), .clr(in_2));
  Register #(.width(1)) register_13 (.D(ALUsrc_in_2), .en(in_3), .Q(ALUsrc_out_2), .clk(in_1), .clr(in_2));
  Register #(.width(1)) register_14 (.D(MemToReg_in_2), .en(in_3), .Q(MemToReg_out_2), .clk(in_1), .clr(in_2));
  Register #(.width(1)) register_15 (.D(RegWrite_in_2), .en(in_3), .Q(RegWrite_out_2), .clk(in_1), .clr(in_2));
  Register #(.width(1)) register_16 (.D(MemRead_in_2), .en(in_3), .Q(MemRead_out_2), .clk(in_1), .clr(in_2));

  // Other names for the same wires on the sheet: clk = in_1; reset = in_2; stall = in_3
endmodule

module ExecMem (
  input  in_1,
  input  in_2,
  input  in_3,
  input  [23:0] in_4,
  input  zero,
  input  [31:0] ALUSUMA,
  input  [31:0] in_7,
  input  [4:0] in_8,
  input  [4:0] rd,
  input  MemToReg_in,
  input  RegWrite_in,
  input  MemRead_in,
  input  MemWrite_in,
  input  Branch_in,
  input  MemToReg_in_2,
  input  RegWrite_in_2,
  input  MemRead_in_2,
  input  MemWrite_in_2,
  input  Branch_in_2,
  input  Branch_in_3,
  input  [23:0] PCinstr,
  output [23:0] AddBranch,
  output Ozero,
  output [31:0] OALUSUMA,
  output [31:0] AddBranch_2,
  output [4:0] out_26,
  output [4:0] rd_2,
  output MemToReg_out,
  output RegWrite_out,
  output MemRead_out,
  output MemWrite_out,
  output Branch_out,
  output MemToReg_out_2,
  output RegWrite_out_2,
  output MemRead_out_2,
  output MemWrite_out_2,
  output Branch_out_2,
  output Branch_out_3,
  output [23:0] PCinstr_2
);

  wire comparator_1_eq, counter_1_q;

  Register #(.width(24)) u_AddBranch (.D(in_4), .en(in_3), .Q(AddBranch), .clk(in_1), .clr(in_2));
  Register #(.width(1)) u_zero (.D(zero), .en(in_3), .Q(Ozero), .clk(in_1), .clr(in_2));
  Register #(.width(32)) u_ALUSUMA (.D(ALUSUMA), .en(in_3), .Q(OALUSUMA), .clk(in_1), .clr(in_2));
  Register #(.width(32)) u_AddBranch_2 (.D(in_7), .en(in_3), .Q(AddBranch_2), .clk(in_1), .clr(in_2));
  Register #(.width(5)) register_1 (.D(in_8), .en(in_3), .Q(out_26), .clk(in_1), .clr(in_2));
  Register #(.width(5)) u_rd (.D(rd), .en(in_3), .Q(rd_2), .clk(in_1), .clr(in_2));
  Register #(.width(1)) register_2 (.D(MemToReg_in), .en(in_3), .Q(MemToReg_out), .clk(in_1), .clr(in_2));
  Register #(.width(1)) register_3 (.D(RegWrite_in), .en(in_3), .Q(RegWrite_out), .clk(in_1), .clr(in_2));
  Register #(.width(1)) register_4 (.D(MemRead_in), .en(in_3), .Q(MemRead_out), .clk(in_1), .clr(in_2));
  Register #(.width(1)) register_5 (.D(MemWrite_in), .en(in_3), .Q(MemWrite_out), .clk(in_1), .clr(in_2));
  Register #(.width(1)) register_6 (.D(Branch_in), .en(in_3), .Q(Branch_out), .clk(in_1), .clr(in_2));
  Register #(.width(1)) register_7 (.D(MemToReg_in_2), .en(in_3), .Q(MemToReg_out_2), .clk(in_1), .clr(in_2));
  Register #(.width(1)) register_8 (.D(RegWrite_in_2), .en(in_3), .Q(RegWrite_out_2), .clk(in_1), .clr(in_2));
  Register #(.width(1)) register_9 (.D(MemRead_in_2), .en(in_3), .Q(MemRead_out_2), .clk(in_1), .clr(in_2));
  Register #(.width(1)) register_10 (.D(MemWrite_in_2), .en(in_3), .Q(MemWrite_out_2), .clk(in_1), .clr(in_2));
  Register #(.width(1)) register_11 (.D(Branch_in_2), .en(in_3), .Q(Branch_out_2), .clk(in_1), .clr(in_2));
  Register #(.width(1)) register_12 (.D(Branch_in_3), .en(in_3), .Q(Branch_out_3), .clk(in_1), .clr(in_2));
  Register #(.width(24)) u_PCinstr (.D(PCinstr), .en(in_3), .Q(PCinstr_2), .clk(in_1), .clr(in_2));
  Counter #(.width(1), .max('h1)) counter_1 (
    .D(1'b1), .Q(counter_1_q), .clk(in_1), .clr(in_3));  // open: load, count, carry
  Comparator #(.width(1)) comparator_1 (.a(1'b1), .b(counter_1_q), .eq(comparator_1_eq));  // open: gt, lt
  Multiplexer multiplexer_1 (.in0(comparator_1_eq), .sel(in_3));  // open: in1, out, en

  // Other names for the same wires on the sheet: clk = in_1; reset = in_2; stall = in_3
endmodule

module MemWB (
  input  in_1,
  input  in_2,
  input  [31:0] in_3,
  input  [31:0] in_4,
  input  [4:0] in_5,
  input  [4:0] in_6,
  input  MemToReg_in,
  input  RegWrite_in,
  input  MemRead_in,
  input  RegWrite_in_2,
  input  MemRead_in_2,
  input  MemToReg_in_2,
  input  RegWrite_in_3,
  input  MemRead_in_3,
  input  MemRead_in_4,
  input  [23:0] in_16,
  output [31:0] out_17,
  output [31:0] out_18,
  output [4:0] out_19,
  output [4:0] out_20,
  output MemToReg_out,
  output RegWrite_out,
  output MemRead_out,
  output RegWrite_out_2,
  output MemRead_out_2,
  output MemToReg_out_2,
  output RegWrite_out_3,
  output MemRead_out_3,
  output MemRead_out_4,
  output [23:0] out_30
);

  Register #(.width(32)) register_1 (.D(in_3), .Q(out_17), .clk(in_1), .clr(in_2));  // open: en
  Register #(.width(32)) register_2 (.D(in_4), .Q(out_18), .clk(in_1), .clr(in_2));  // open: en
  Register #(.width(5)) register_3 (.D(in_5), .Q(out_19), .clk(in_1), .clr(in_2));  // open: en
  Register #(.width(5)) register_4 (.D(in_6), .Q(out_20), .clk(in_1), .clr(in_2));  // open: en
  Register #(.width(1)) register_5 (.D(MemToReg_in), .Q(MemToReg_out), .clk(in_1), .clr(in_2));  // open: en
  Register #(.width(1)) register_6 (.D(RegWrite_in), .Q(RegWrite_out), .clk(in_1), .clr(in_2));  // open: en
  Register #(.width(1)) register_7 (.D(MemRead_in), .Q(MemRead_out), .clk(in_1), .clr(in_2));  // open: en
  Register #(.width(1)) register_8 (.D(RegWrite_in_2), .Q(RegWrite_out_2), .clk(in_1), .clr(in_2));  // open: en
  Register #(.width(1)) register_9 (.D(MemRead_in_2), .Q(MemRead_out_2), .clk(in_1), .clr(in_2));  // open: en
  Register #(.width(1)) register_10 (.D(MemToReg_in_2), .Q(MemToReg_out_2), .clk(in_1), .clr(in_2));  // open: en
  Register #(.width(1)) register_11 (.D(RegWrite_in_3), .Q(RegWrite_out_3), .clk(in_1), .clr(in_2));  // open: en
  Register #(.width(1)) register_12 (.D(MemRead_in_3), .Q(MemRead_out_3), .clk(in_1), .clr(in_2));  // open: en
  Register #(.width(1)) register_13 (.D(MemRead_in_4), .Q(MemRead_out_4), .clk(in_1), .clr(in_2));  // open: en
  Register #(.width(24)) register_14 (.D(in_16), .Q(out_30), .clk(in_1), .clr(in_2));  // open: en

  // Other names for the same wires on the sheet: clk = in_1; reset = in_2
endmodule

module ExHazard (
  input  ExMemRegWr,
  input  [4:0] ExMemRd,
  input  [4:0] IDExcRs,
  input  [4:0] IDExcRt,
  input  MemWbRegWr,
  input  [4:0] MemWbRd,
  output [1:0] ForwardA,
  output forward,
  output [1:0] ForwardB
);

  wire comparator_1_eq, comparator_2_eq, comparator_3_eq, comparator_4_eq, comparator_5_eq, comparator_6_eq,
       comparator_7_eq, comparator_8_eq, not_1_out, not_2_out, not_3_out, not_4_out;

  Comparator #(.width(5)) comparator_1 (.a(ExMemRd), .b({5{1'b0}}), .eq(comparator_1_eq));  // open: gt, lt
  Comparator #(.width(5)) comparator_2 (.a(ExMemRd), .b(IDExcRs), .eq(comparator_2_eq));  // open: gt, lt
  Comparator #(.width(5)) comparator_3 (.a(ExMemRd), .b(IDExcRt), .eq(comparator_3_eq));  // open: gt, lt
  Comparator #(.width(5)) comparator_4 (.a({5{1'b0}}), .b(MemWbRd), .eq(comparator_4_eq));  // open: gt, lt
  Comparator #(.width(5)) comparator_5 (.a(ExMemRd), .b(IDExcRs), .eq(comparator_5_eq));  // open: gt, lt
  Comparator #(.width(5)) comparator_6 (.a(MemWbRd), .b(IDExcRs), .eq(comparator_6_eq));  // open: gt, lt
  Comparator #(.width(5)) comparator_7 (.a(ExMemRd), .b(IDExcRt), .eq(comparator_7_eq));  // open: gt, lt
  not not_1 (not_1_out, comparator_7_eq);
  Comparator #(.width(5)) comparator_8 (.a(MemWbRd), .b(IDExcRt), .eq(comparator_8_eq));  // open: gt, lt
  not not_2 (not_2_out, comparator_1_eq);
  not not_3 (not_3_out, comparator_4_eq);
  not not_4 (not_4_out, comparator_5_eq);
  and and_1 (ForwardA[1], ExMemRegWr, not_2_out, comparator_2_eq);
  and and_2 (ForwardB[1], ExMemRegWr, not_2_out, comparator_3_eq);
  and and_3 (ForwardA[0], MemWbRegWr, not_3_out, not_4_out, comparator_6_eq);
  and and_4 (ForwardB[0], MemWbRegWr, not_3_out, not_1_out, comparator_8_eq);
  or or_1 (forward, ForwardA[1], ForwardB[1], ForwardA[0], ForwardB[0]);

  // Other names for the same wires on the sheet: esMemRd[4:0] = ExMemRd; idExRs[4:0] = IDExcRs; idExRt[4:0] = IDExcRt
endmodule

module HazardControl (
  input  [23:0] pc_ExcMem,
  input  [23:0] pc_Memwb,
  input  Hazard,
  output out_4,
  output enable
);

  wire comparator_1_eq, comparator_2_eq, not_1_out;

  Comparator #(.width(24)) comparator_1 (.a(pc_ExcMem), .b({24{1'b0}}), .eq(comparator_1_eq));  // open: gt, lt
  not not_1 (not_1_out, comparator_2_eq);
  Comparator #(.width(24)) comparator_2 (.a(pc_Memwb), .b(pc_ExcMem), .eq(comparator_2_eq));  // open: gt, lt
  and and_1 (out_4, not_1_out, comparator_1_eq);
  or or_1 (enable, out_4, Hazard);
endmodule

module mostrarInst (
  input  ADD,
  input  ADDI,
  input  STALL,
  input  BRANCH,
  input  JUMP,
  input  LOAD,
  input  STORE,
  output [31:0] out_8,
  output [31:0] out_9,
  output [31:0] out_10,
  output [31:0] out_11,
  output [31:0] out_12
);

  wire [2:0] Slct;

  BitFinder #(.\type ("high1")) bitfinder_1 (
    .in({STORE, LOAD, JUMP, BRANCH, STALL, ADDI, ADD, 1'b0}), .index(Slct));  // open: found
  Multiplexer #(.select(3), .width(32), .enable("false")) multiplexer_1 (
    .in0({32{1'b0}}), .in1(32'h67380000), .in2(32'h67390000), .in3(32'h6319e000), .in4(32'h7798ce90),
    .in5(32'hfa58b800), .in6(32'h8f19c000), .in7(32'h6f98c780), .out(out_8), .sel(Slct));
  Multiplexer #(.select(3), .width(32), .enable("false")) multiplexer_2 (
    .in0({32{1'b0}}), .in1(32'h94a40000), .in2(32'h94a50000), .in3(32'h94a51000), .in4(32'h94a52890),
    .in5(32'h2255a400), .in6(32'h89252000), .in7(32'h82252400), .out(out_9), .sel(Slct));
  Multiplexer #(.select(3), .width(32), .enable("false")) multiplexer_3 (
    .in0({32{1'b0}}), .in1(32'h94a40000), .in2(32'h94a50000), .in3(32'h94a5f000), .in4(32'hf72528f0),
    .in5(32'h2252b800), .in6(32'h89252000), .in7(32'h62254780), .out(out_10), .sel(Slct));
  Multiplexer #(.select(3), .width(32), .enable("false")) multiplexer_4 (
    .in0({32{1'b0}}), .in1(32'hf4a40000), .in2(32'hf4a50000), .in3(32'h94a50000), .in4(32'h953d2890),
    .in5(32'h2250a000), .in6(32'h893d2000), .in7(32'h12252400), .out(out_11), .sel(Slct));
  Multiplexer #(.select(3), .width(32), .enable("false")) multiplexer_5 (
    .in0({32{1'b0}}), .in1(32'h97bc0000), .in2(32'h97bd0000), .in3(32'h93190000), .in4(32'hf4a52e90),
    .in5(32'he190a000), .in6(32'hef25e000), .in7(32'he2191780), .out(out_12), .sel(Slct));
endmodule

module mostrarDisplay (
  input  [23:0] in_1,
  output out_2,
  output out_3,
  output out_4,
  output out_5,
  output out_6,
  output out_7,
  output out_8,
  output out_9
);

  wire [3:0] casilla;

  Bit_Extender #(.in_width(24), .out_width(4)) bit_extender_1 (.in(in_1), .out(casilla));
  Multiplexer #(.select(4), .enable("false")) multiplexer_1 (
    .in0(1'b0), .in1(1'b0), .in2(1'b1), .in3(1'b1), .in4(1'b1), .in5(1'b1), .in6(1'b1), .in7(1'b1),
    .in8(1'b1), .in9(1'b1), .out(out_2), .sel(casilla));  // open: in10, in11, in12, in13, in14, in15
  Multiplexer #(.select(4), .enable("false")) multiplexer_2 (
    .in0(1'b1), .in1(1'b0), .in2(1'b0), .in3(1'b0), .in4(1'b1), .in5(1'b1), .in6(1'b1), .in7(1'b0),
    .in8(1'b1), .in9(1'b1), .out(out_3), .sel(casilla));  // open: in10, in11, in12, in13, in14, in15
  Multiplexer #(.select(4), .enable("false")) multiplexer_3 (
    .in0(1'b1), .in1(1'b0), .in2(1'b1), .in3(1'b1), .in4(1'b0), .in5(1'b1), .in6(1'b1), .in7(1'b1),
    .in8(1'b1), .in9(1'b1), .out(out_4), .sel(casilla));  // open: in10, in11, in12, in13, in14, in15
  Multiplexer #(.select(4), .enable("false")) multiplexer_4 (
    .in0(1'b1), .in1(1'b1), .in2(1'b1), .in3(1'b1), .in4(1'b1), .in5(1'b0), .in6(1'b0), .in7(1'b1),
    .in8(1'b1), .in9(1'b1), .out(out_5), .sel(casilla));  // open: in10, in11, in12, in13, in14, in15
  Multiplexer #(.select(4), .enable("false")) multiplexer_5 (
    .in0(1'b1), .in1(1'b0), .in2(1'b1), .in3(1'b0), .in4(1'b0), .in5(1'b0), .in6(1'b1), .in7(1'b0),
    .in8(1'b1), .in9(1'b0), .out(out_6), .sel(casilla));  // open: in10, in11, in12, in13, in14, in15
  Multiplexer #(.select(4), .enable("false")) multiplexer_6 (
    .in0(1'b1), .in1(1'b0), .in2(1'b1), .in3(1'b1), .in4(1'b0), .in5(1'b1), .in6(1'b1), .in7(1'b0),
    .in8(1'b1), .in9(1'b1), .out(out_7), .sel(casilla));  // open: in10, in11, in12, in13, in14, in15
  Multiplexer #(.select(4), .enable("false")) multiplexer_7 (
    .in0(1'b1), .in1(1'b1), .in2(1'b0), .in3(1'b1), .in4(1'b1), .in5(1'b1), .in6(1'b1), .in7(1'b1),
    .in8(1'b1), .in9(1'b1), .out(out_8), .sel(casilla));  // open: in10, in11, in12, in13, in14, in15
  Multiplexer #(.select(4), .enable("false")) multiplexer_8 (
    .in0(1'b1), .in1(1'b0), .in2(1'b1), .in3(1'b1), .in4(1'b1), .in5(1'b1), .in6(1'b1), .in7(1'b1),
    .in8(1'b1), .in9(1'b1), .out(out_9), .sel(casilla));  // open: in10, in11, in12, in13, in14, in15
endmodule

module IDhazard (
  input  IDEXMemRead,
  input  [4:0] IDEXRt,
  input  [4:0] IFIDRs,
  input  [4:0] IFIDRt,
  output stall
);

  wire comparator_1_eq, comparator_2_eq, or_1_out;

  Comparator #(.width(5)) comparator_1 (.a(IDEXRt), .b(IFIDRs), .eq(comparator_1_eq));  // open: gt, lt
  Comparator #(.width(5)) comparator_2 (.a(IDEXRt), .b(IFIDRt), .eq(comparator_2_eq));  // open: gt, lt
  or or_1 (or_1_out, comparator_1_eq, comparator_2_eq);
  and and_1 (stall, IDEXMemRead, or_1_out);
endmodule

module DIS (
  input  CONST,
  input  [23:0] PC,
  output [3:0] DEC,
  output [3:0] UNIT
);

  wire and_1_out, and_2_out, and_3_out, and_4_out, and_5_out, and_6_out, and_7_out, and_8_out, and_9_out,
       and_10_out, not_1_out, not_2_out, not_3_out, not_4_out, not_5_out, not_6_out, not_7_out, not_8_out;
  wire [0:0] or_1_out;
  wire [3:1] or_4_out;

  and and_1 (and_1_out, PC[3], PC[1]);
  and and_2 (and_2_out, PC[3], PC[2]);
  not not_1 (not_1_out, PC[2]);
  not not_2 (not_2_out, PC[1]);
  not not_3 (not_3_out, PC[3]);
  not not_4 (not_4_out, PC[1]);
  not not_5 (not_5_out, PC[4]);
  not not_6 (not_6_out, PC[3]);
  not not_7 (not_7_out, PC[1]);
  not not_8 (not_8_out, PC[1]);
  or or_1 (or_1_out[0], and_1_out, and_2_out, PC[4]);
  and and_3 (and_3_out, PC[3], not_1_out, not_2_out);
  and and_4 (and_4_out, PC[4], PC[1]);
  and and_5 (and_5_out, not_3_out, PC[2]);
  and and_6 (and_6_out, PC[2], PC[1]);
  and and_7 (and_7_out, PC[4], not_4_out);
  and and_8 (and_8_out, not_5_out, not_6_out, PC[1]);
  and and_9 (and_9_out, PC[3], PC[2], not_7_out);
  and and_10 (and_10_out, PC[4], not_8_out);
  or or_2 (or_4_out[3], and_3_out, and_4_out);
  or or_3 (or_4_out[2], and_5_out, and_6_out, and_7_out);
  or or_4 (or_4_out[1], and_8_out, and_9_out, and_10_out);
  Hex_Digit_Display hex_digit_display_1 (.value(DEC));  // open: dp
  Multiplexer #(.width(4)) multiplexer_1 (
    .in0(4'b1110), .in1({3'b000, or_1_out[0]}), .out(DEC), .sel(CONST));  // open: en
  Multiplexer #(.width(4)) multiplexer_2 (.in0(4'b1110), .in1({or_4_out, PC[0]}), .out(UNIT), .sel(CONST));  // open: en
  Hex_Digit_Display hex_digit_display_2 (.value(UNIT));  // open: dp
endmodule
